// Logisim project ALU_modular_design.circ as structural Verilog
module ALU_1bit (
  input  A,
  input  B,
  input  SUB,
  input  Cin,
  input  SEL0,
  input  SEL1,
  output Cout_output,
  output out_8
);

  wire AND_out_out, Beff_out, OR_out_out, SUM_out, t1_out, t2_out, X_out, XOR_out_out;

  and AND_out (AND_out_out, A, B);
  or OR_out (OR_out_out, A, B);
  xor XOR_out (XOR_out_out, A, B);
  xor Beff (Beff_out, B, SUB);
  xor X (X_out, A, Beff_out);
  and t1 (t1_out, A, Beff_out);
  and t2 (t2_out, X_out, Cin);
  xor SUM (SUM_out, X_out, Cin);
  or Cout (Cout_output, t1_out, t2_out);
  mux_4_to_1 mux_4_to_1_1 (
    .A(AND_out_out), .B(OR_out_out), .C(SUM_out), .D(XOR_out_out), .SEL_0(SEL0), .SEL_1(SEL1), .Q(out_8));
endmodule

module main (
  input  A_0,
  input  A_1,
  input  A_2,
  input  A_3,
  input  B_0,
  input  B_1,
  input  B_2,
  input  B_3,
  input  SUB,
  input  SEL0,
  input  SEL1,
  input  in_12,
  input  in_13,
  input  in_14,
  input  in_15,
  input  in_16,
  input  in_17,
  input  in_18,
  input  in_19,
  input  [1:0] in_20,
  input  in_21,
  input  [1:0] in_22,
  input  [1:0] in_23,
  input  in_24,
  input  in_25,
  input  in_26,
  input  in_27,
  input  in_28,
  input  in_29,
  input  in_30,
  input  in_31,
  input  in_32,
  input  in_33,
  input  in_34,
  input  in_35,
  input  in_36,
  input  in_37,
  input  in_38,
  input  in_39,
  input  in_40,
  input  in_41,
  input  in_42,
  input  in_43,
  input  in_44,
  input  in_45,
  input  in_46,
  input  in_47,
  input  in_48,
  input  in_49,
  input  in_50,
  input  in_51,
  input  in_52,
  input  in_53,
  input  in_54,
  input  in_55,
  input  in_56,
  input  in_57,
  input  in_58,
  input  in_59,
  input  in_60,
  input  in_61,
  input  in_62,
  input  in_63,
  input  in_64,
  input  in_65,
  input  in_66,
  input  in_67,
  input  in_68,
  input  in_69,
  input  in_70,
  input  in_71,
  input  in_72,
  input  in_73,
  output out_74,
  output out_75,
  output out_76,
  output out_77,
  output out_78,
  output out_79,
  output out_80,
  output out_81,
  output out_82,
  output out_83,
  output out_84,
  output out_85,
  output out_86,
  output out_87,
  output out_88,
  output out_89,
  output out_90,
  output out_91,
  output out_92,
  output out_93,
  output out_94,
  output out_95,
  output out_96,
  output out_97,
  output out_98,
  output out_99,
  output out_100,
  output out_101,
  output out_102,
  output out_103,
  output out_104,
  output out_105,
  output out_106
);

  wire alu_1bit_1_cout_output, alu_1bit_2_cout_output, alu_1bit_3_cout_output, alu_1bit_4_cout_output,
       alu_1bit_5_cout_output, alu_1bit_6_cout_output, alu_1bit_7_cout_output, alu_1bit_8_cout_output,
       alu_1bit_9_cout_output, alu_1bit_10_cout_output, alu_1bit_11_cout_output, alu_1bit_12_cout_output,
       alu_1bit_13_cout_output, alu_1bit_14_cout_output, alu_1bit_15_cout_output, alu_1bit_16_cout_output,
       alu_1bit_17_cout_output, alu_1bit_18_cout_output, alu_1bit_19_cout_output, alu_1bit_20_cout_output,
       alu_1bit_21_cout_output, alu_1bit_22_cout_output, alu_1bit_23_cout_output, alu_1bit_24_cout_output,
       alu_1bit_25_cout_output, alu_1bit_26_cout_output, alu_1bit_27_cout_output, alu_1bit_28_cout_output,
       alu_1bit_29_cout_output, alu_1bit_30_cout_output, alu_1bit_31_cout_output, CLK_out, nor_1_out,
       overflow_flag_1_out_5, register_1_q, register_2_q, register_3_q, undriven_2;
  wire [3:0] or_1_out, reg4x32file_1_rd_a, reg4x32file_1_rd_a_2, reg4x32file_1_rd_a_3, reg4x32file_1_rd_a_4,
       reg4x32file_1_rd_a_5, reg4x32file_1_rd_a_6, reg4x32file_1_rd_a_7, reg4x32file_1_rd_a_8,
       reg4x32file_1_rd_b, reg4x32file_1_rd_b_2, reg4x32file_1_rd_b_3, reg4x32file_1_rd_b_4,
       reg4x32file_1_rd_b_5, reg4x32file_1_rd_b_6, reg4x32file_1_rd_b_7, reg4x32file_1_rd_b_8;
  wire [31:0] multiplexer_1_out, multiplexer_2_out, undriven;

  Multiplexer #(.width(32)) multiplexer_1 (
    .in0(multiplexer_2_out), .in1(undriven), .out(multiplexer_1_out), .sel(in_32));
  Hex_Digit_Display hex_digit_display_1 (.value(reg4x32file_1_rd_a_8));  // open: dp
  Hex_Digit_Display hex_digit_display_2 (.value(reg4x32file_1_rd_b_8));  // open: dp
  Hex_Digit_Display hex_digit_display_3 (.value(undriven[31:28]));  // open: dp
  Hex_Digit_Display hex_digit_display_4 (.value(reg4x32file_1_rd_a_7));  // open: dp
  Hex_Digit_Display hex_digit_display_5 (.value(reg4x32file_1_rd_a_6));  // open: dp
  Hex_Digit_Display hex_digit_display_6 (.value(reg4x32file_1_rd_b_7));  // open: dp
  Hex_Digit_Display hex_digit_display_7 (.value(reg4x32file_1_rd_b_6));  // open: dp
  Hex_Digit_Display hex_digit_display_8 (.value(undriven[27:24]));  // open: dp
  Hex_Digit_Display hex_digit_display_9 (.value(undriven[23:20]));  // open: dp
  Multiplexer #(.width(32)) multiplexer_2 (
    .in0({in_69, in_68, in_67, in_66, in_61, in_60, in_59, in_58, in_53, in_52, in_51, in_50, in_45, in_44, in_43, in_42, in_37, in_36, in_35, in_34, in_27, in_26, in_25, in_24, in_15, in_14, in_13, in_12, A_3, A_2, A_1, A_0}),
    .in1({in_73, in_72, in_71, in_70, in_65, in_64, in_63, in_62, in_57, in_56, in_55, in_54, in_49, in_48, in_47, in_46, in_41, in_40, in_39, in_38, in_31, in_30, in_29, in_28, in_19, in_18, in_17, in_16, B_3, B_2, B_1, B_0}),
    .out(multiplexer_2_out), .sel(in_33));
  Hex_Digit_Display hex_digit_display_10 (.value(reg4x32file_1_rd_a_5));  // open: dp
  Hex_Digit_Display hex_digit_display_11 (.value(reg4x32file_1_rd_a_4));  // open: dp
  Hex_Digit_Display hex_digit_display_12 (.value(reg4x32file_1_rd_b_5));  // open: dp
  Hex_Digit_Display hex_digit_display_13 (.value(reg4x32file_1_rd_b_4));  // open: dp
  Hex_Digit_Display hex_digit_display_14 (.value(undriven[19:16]));  // open: dp
  Hex_Digit_Display hex_digit_display_15 (.value(undriven[15:12]));  // open: dp
  Hex_Digit_Display hex_digit_display_16 (.value(reg4x32file_1_rd_a_3));  // open: dp
  Hex_Digit_Display hex_digit_display_17 (.value(reg4x32file_1_rd_a_2));  // open: dp
  Hex_Digit_Display hex_digit_display_18 (.value(reg4x32file_1_rd_b_3));  // open: dp
  Hex_Digit_Display hex_digit_display_19 (.value(reg4x32file_1_rd_b_2));  // open: dp
  Hex_Digit_Display hex_digit_display_20 (.value(undriven[11:8]));  // open: dp
  Hex_Digit_Display hex_digit_display_21 (.value(undriven[7:4]));  // open: dp
  Hex_Digit_Display hex_digit_display_22 (.value(reg4x32file_1_rd_a));  // open: dp
  Hex_Digit_Display hex_digit_display_23 (.value(reg4x32file_1_rd_b));  // open: dp
  Hex_Digit_Display hex_digit_display_24 (.value(undriven[3:0]));  // open: dp
  reg4x32file reg4x32file_1 (
    .CLK(CLK_out), .WA(in_20), .WD(multiplexer_1_out), .WE(in_21), .RA(in_22), .RB(in_23),
    .RD_A({reg4x32file_1_rd_a_8, reg4x32file_1_rd_a_7, reg4x32file_1_rd_a_6, reg4x32file_1_rd_a_5, reg4x32file_1_rd_a_4, reg4x32file_1_rd_a_3, reg4x32file_1_rd_a_2, reg4x32file_1_rd_a}),
    .RD_B({reg4x32file_1_rd_b_8, reg4x32file_1_rd_b_7, reg4x32file_1_rd_b_6, reg4x32file_1_rd_b_5, reg4x32file_1_rd_b_4, reg4x32file_1_rd_b_3, reg4x32file_1_rd_b_2, reg4x32file_1_rd_b}));
  // Probe on {reg4x32file_1_rd_b_8, reg4x32file_1_rd_b_7, reg4x32file_1_rd_b_6, reg4x32file_1_rd_b_5, reg4x32file_1_rd_b_4, reg4x32file_1_rd_b_3, reg4x32file_1_rd_b_2, reg4x32file_1_rd_b}
  // Probe on {reg4x32file_1_rd_a_8, reg4x32file_1_rd_a_7, reg4x32file_1_rd_a_6, reg4x32file_1_rd_a_5, reg4x32file_1_rd_a_4, reg4x32file_1_rd_a_3, reg4x32file_1_rd_a_2, reg4x32file_1_rd_a}
  LED led_1 (.in(undriven[31]));
  LED led_2 (.in(undriven[30]));
  LED led_3 (.in(reg4x32file_1_rd_a_8[3]));
  LED led_4 (.in(undriven[29]));
  LED led_5 (.in(undriven[28]));
  LED led_6 (.in(reg4x32file_1_rd_a_8[2]));
  LED led_7 (.in(reg4x32file_1_rd_a_8[1]));
  Clock CLK (.out(CLK_out));
  LED led_8 (.in(reg4x32file_1_rd_b_8[3]));
  LED led_9 (.in(reg4x32file_1_rd_a_8[0]));
  overflow_flag overflow_flag_1 (
    .B_MSB(reg4x32file_1_rd_b_8[3]), .A_MSB(reg4x32file_1_rd_a_8[3]), .R_MSB(undriven[31]), .OP(SUB),
    .out_5(overflow_flag_1_out_5));
  LED led_10 (.in(reg4x32file_1_rd_b_8[2]));
  LED led_11 (.in(reg4x32file_1_rd_b_8[1]));
  Register #(.width(1)) register_1 (.D(overflow_flag_1_out_5), .clk(CLK_out), .Q(register_1_q));  // open: en, clr
  LED led_12 (.in(reg4x32file_1_rd_b_8[0]));
  assign or_1_out = undriven[31:28] | undriven[27:24] | undriven[23:20] | undriven[19:16] | undriven[15:12] | undriven[11:8] | undriven[7:4] | undriven[3:0];  // OR_Gate or_1, 4 bits wide
  _7_Segment_Display u_7_segment_display_1 (
    .f(register_1_q), .b(register_1_q), .e(register_1_q), .d(register_1_q), .c(register_1_q));  // open: g, a, dp
  nor nor_1 (nor_1_out, or_1_out[3], or_1_out[2], or_1_out[1], or_1_out[0]);
  _7_Segment_Display u_7_segment_display_2 (
    .f(nor_1_out), .a(nor_1_out), .b(nor_1_out), .e(nor_1_out), .d(nor_1_out), .c(nor_1_out), .dp(nor_1_out));  // open: g
  _7_Segment_Display u_7_segment_display_3 (.g(register_3_q));  // open: f, a, b, e, d, c, dp
  Register #(.width(1)) register_2 (.D(out_102), .clk(CLK_out), .Q(register_2_q));  // open: en, clr
  _7_Segment_Display u_7_segment_display_4 (
    .f(register_2_q), .a(register_2_q), .e(register_2_q), .d(register_2_q));  // open: g, b, c, dp
  Register #(.width(1)) register_3 (.D(undriven_2), .clk(CLK_out), .Q(register_3_q));  // open: en, clr
  ALU_1bit alu_1bit_1 (
    .A(A_0), .B(B_0), .SUB(SUB), .Cin(SUB), .SEL0(SEL0), .SEL1(SEL1), .Cout_output(alu_1bit_1_cout_output),
    .out_8(out_74));
  ALU_1bit alu_1bit_2 (
    .A(in_12), .B(in_16), .SUB(SUB), .Cin(alu_1bit_25_cout_output), .SEL0(SEL0), .SEL1(SEL1),
    .Cout_output(alu_1bit_2_cout_output), .out_8(out_78));
  ALU_1bit alu_1bit_3 (
    .A(in_24), .B(in_28), .SUB(SUB), .Cin(alu_1bit_26_cout_output), .SEL0(SEL0), .SEL1(SEL1),
    .Cout_output(alu_1bit_3_cout_output), .out_8(out_82));
  ALU_1bit alu_1bit_4 (
    .A(in_34), .B(in_38), .SUB(SUB), .Cin(alu_1bit_27_cout_output), .SEL0(SEL0), .SEL1(SEL1),
    .Cout_output(alu_1bit_4_cout_output), .out_8(out_86));
  ALU_1bit alu_1bit_5 (
    .A(in_42), .B(in_46), .SUB(SUB), .Cin(alu_1bit_28_cout_output), .SEL0(SEL0), .SEL1(SEL1),
    .Cout_output(alu_1bit_5_cout_output), .out_8(out_90));
  ALU_1bit alu_1bit_6 (
    .A(in_50), .B(in_54), .SUB(SUB), .Cin(alu_1bit_29_cout_output), .SEL0(SEL0), .SEL1(SEL1),
    .Cout_output(alu_1bit_6_cout_output), .out_8(out_94));
  ALU_1bit alu_1bit_7 (
    .A(in_58), .B(in_62), .SUB(SUB), .Cin(alu_1bit_30_cout_output), .SEL0(SEL0),
    .Cout_output(alu_1bit_7_cout_output), .out_8(out_98));  // open: SEL1
  ALU_1bit alu_1bit_8 (
    .A(in_66), .B(in_70), .SUB(SUB), .Cin(alu_1bit_31_cout_output), .SEL0(SEL0), .SEL1(SEL1),
    .Cout_output(alu_1bit_8_cout_output), .out_8(out_103));
  ALU_1bit alu_1bit_9 (
    .A(A_1), .B(B_1), .SUB(SUB), .Cin(alu_1bit_1_cout_output), .SEL0(SEL0), .SEL1(SEL1),
    .Cout_output(alu_1bit_9_cout_output), .out_8(out_75));
  ALU_1bit alu_1bit_10 (
    .A(in_13), .B(in_17), .SUB(SUB), .Cin(alu_1bit_2_cout_output), .SEL0(SEL0), .SEL1(SEL1),
    .Cout_output(alu_1bit_10_cout_output), .out_8(out_79));
  ALU_1bit alu_1bit_11 (
    .A(in_25), .B(in_29), .SUB(SUB), .Cin(alu_1bit_3_cout_output), .SEL0(SEL0), .SEL1(SEL1),
    .Cout_output(alu_1bit_11_cout_output), .out_8(out_83));
  ALU_1bit alu_1bit_12 (
    .A(in_35), .B(in_39), .SUB(SUB), .Cin(alu_1bit_4_cout_output), .SEL0(SEL0), .SEL1(SEL1),
    .Cout_output(alu_1bit_12_cout_output), .out_8(out_87));
  ALU_1bit alu_1bit_13 (
    .A(in_43), .B(in_47), .SUB(SUB), .Cin(alu_1bit_5_cout_output), .SEL0(SEL0), .SEL1(SEL1),
    .Cout_output(alu_1bit_13_cout_output), .out_8(out_91));
  ALU_1bit alu_1bit_14 (
    .A(in_51), .B(in_55), .SUB(SUB), .Cin(alu_1bit_6_cout_output), .SEL0(SEL0), .SEL1(SEL1),
    .Cout_output(alu_1bit_14_cout_output), .out_8(out_95));
  ALU_1bit alu_1bit_15 (
    .A(in_59), .B(in_63), .SUB(SUB), .Cin(alu_1bit_7_cout_output), .SEL0(SEL0),
    .Cout_output(alu_1bit_15_cout_output), .out_8(out_99));  // open: SEL1
  ALU_1bit alu_1bit_16 (
    .A(in_67), .B(in_71), .SUB(SUB), .Cin(alu_1bit_8_cout_output), .SEL0(SEL0), .SEL1(SEL1),
    .Cout_output(alu_1bit_16_cout_output), .out_8(out_104));
  ALU_1bit alu_1bit_17 (
    .A(A_2), .B(B_2), .SUB(SUB), .Cin(alu_1bit_9_cout_output), .SEL0(SEL0), .SEL1(SEL1),
    .Cout_output(alu_1bit_17_cout_output), .out_8(out_76));
  ALU_1bit alu_1bit_18 (
    .A(in_14), .B(in_18), .SUB(SUB), .Cin(alu_1bit_10_cout_output), .SEL0(SEL0), .SEL1(SEL1),
    .Cout_output(alu_1bit_18_cout_output), .out_8(out_80));
  ALU_1bit alu_1bit_19 (
    .A(in_26), .B(in_30), .SUB(SUB), .Cin(alu_1bit_11_cout_output), .SEL0(SEL0), .SEL1(SEL1),
    .Cout_output(alu_1bit_19_cout_output), .out_8(out_84));
  ALU_1bit alu_1bit_20 (
    .A(in_36), .B(in_40), .SUB(SUB), .Cin(alu_1bit_12_cout_output), .SEL0(SEL0), .SEL1(SEL1),
    .Cout_output(alu_1bit_20_cout_output), .out_8(out_88));
  ALU_1bit alu_1bit_21 (
    .A(in_44), .B(in_48), .SUB(SUB), .Cin(alu_1bit_13_cout_output), .SEL0(SEL0), .SEL1(SEL1),
    .Cout_output(alu_1bit_21_cout_output), .out_8(out_92));
  ALU_1bit alu_1bit_22 (
    .A(in_52), .B(in_56), .SUB(SUB), .Cin(alu_1bit_14_cout_output), .SEL0(SEL0), .SEL1(SEL1),
    .Cout_output(alu_1bit_22_cout_output), .out_8(out_96));
  ALU_1bit alu_1bit_23 (
    .A(in_60), .B(in_64), .SUB(SUB), .Cin(alu_1bit_15_cout_output), .SEL0(SEL0), .SEL1(SEL1),
    .Cout_output(alu_1bit_23_cout_output), .out_8(out_100));
  ALU_1bit alu_1bit_24 (
    .A(in_68), .B(in_72), .SUB(SUB), .Cin(alu_1bit_16_cout_output), .SEL0(SEL0), .SEL1(SEL1),
    .Cout_output(alu_1bit_24_cout_output), .out_8(out_105));
  ALU_1bit alu_1bit_25 (
    .A(A_3), .B(B_3), .SUB(SUB), .Cin(alu_1bit_17_cout_output), .SEL0(SEL0), .SEL1(SEL1),
    .Cout_output(alu_1bit_25_cout_output), .out_8(out_77));
  ALU_1bit alu_1bit_26 (
    .A(in_15), .B(in_19), .SUB(SUB), .Cin(alu_1bit_18_cout_output), .SEL0(SEL0), .SEL1(SEL1),
    .Cout_output(alu_1bit_26_cout_output), .out_8(out_81));
  ALU_1bit alu_1bit_27 (
    .A(in_27), .B(in_31), .SUB(SUB), .Cin(alu_1bit_19_cout_output), .SEL0(SEL0), .SEL1(SEL1),
    .Cout_output(alu_1bit_27_cout_output), .out_8(out_85));
  ALU_1bit alu_1bit_28 (
    .A(in_37), .B(in_41), .SUB(SUB), .Cin(alu_1bit_20_cout_output), .SEL0(SEL0), .SEL1(SEL1),
    .Cout_output(alu_1bit_28_cout_output), .out_8(out_89));
  ALU_1bit alu_1bit_29 (
    .A(in_45), .B(in_49), .SUB(SUB), .Cin(alu_1bit_21_cout_output), .SEL0(SEL0), .SEL1(SEL1),
    .Cout_output(alu_1bit_29_cout_output), .out_8(out_93));
  ALU_1bit alu_1bit_30 (
    .A(in_53), .B(in_57), .SUB(SUB), .Cin(alu_1bit_22_cout_output), .SEL0(SEL0), .SEL1(SEL1),
    .Cout_output(alu_1bit_30_cout_output), .out_8(out_97));
  ALU_1bit alu_1bit_31 (
    .A(in_61), .B(in_65), .SUB(SUB), .Cin(alu_1bit_23_cout_output), .SEL0(SEL0), .SEL1(SEL1),
    .Cout_output(alu_1bit_31_cout_output), .out_8(out_101));
  ALU_1bit alu_1bit_32 (
    .A(in_69), .B(in_73), .SUB(SUB), .Cin(alu_1bit_24_cout_output), .SEL0(SEL0), .SEL1(SEL1),
    .Cout_output(out_102), .out_8(out_106));
endmodule

module mux_4_to_1 (
  input  A,
  input  B,
  input  C,
  input  D,
  input  SEL_0,
  input  SEL_1,
  output Q
);

  wire nand_1_out, nand_2_out, nand_3_out, nand_4_out, nand_5_out, nand_6_out;

  nand nand_1 (nand_1_out, SEL_0, SEL_0);
  nand nand_2 (nand_2_out, SEL_1, SEL_1);
  nand nand_3 (nand_3_out, A, nand_1_out, nand_2_out);
  nand nand_4 (nand_4_out, B, nand_1_out, SEL_1);
  nand nand_5 (nand_5_out, C, nand_2_out, SEL_0);
  nand nand_6 (nand_6_out, D, SEL_0, SEL_1);
  nand nand_7 (Q, nand_3_out, nand_4_out, nand_5_out, nand_6_out);
endmodule

module reg32bit (
  input  A0,
  input  A1,
  input  A2,
  input  A3,
  input  B0,
  input  B1,
  input  B2,
  input  B3,
  input  SEL,
  input  CLK,
  input  in_11,
  input  in_12,
  input  in_13,
  input  in_14,
  input  in_15,
  input  in_16,
  input  in_17,
  input  in_18,
  input  in_19,
  input  in_20,
  input  in_21,
  input  in_22,
  input  in_23,
  input  in_24,
  input  in_25,
  input  in_26,
  input  in_27,
  input  in_28,
  input  in_29,
  input  in_30,
  input  in_31,
  input  in_32,
  input  in_33,
  input  in_34,
  input  in_35,
  input  in_36,
  input  in_37,
  input  in_38,
  input  in_39,
  input  in_40,
  input  in_41,
  input  in_42,
  input  in_43,
  input  in_44,
  input  in_45,
  input  in_46,
  input  in_47,
  input  in_48,
  input  in_49,
  input  in_50,
  input  in_51,
  input  in_52,
  input  in_53,
  input  in_54,
  input  in_55,
  input  in_56,
  input  in_57,
  input  in_58,
  input  in_59,
  input  in_60,
  input  in_61,
  input  in_62,
  input  in_63,
  input  in_64,
  input  in_65,
  input  in_66,
  output Q_0,
  output Q_1,
  output Q_2,
  output Q_3,
  output Q_0_not,
  output Q_1_not,
  output Q_2_not,
  output Q_3_not,
  output out_75,
  output out_76,
  output out_77,
  output out_78,
  output out_79,
  output out_80,
  output out_81,
  output out_82,
  output out_83,
  output out_84,
  output out_85,
  output out_86,
  output out_87,
  output out_88,
  output out_89,
  output out_90,
  output out_91,
  output out_92,
  output out_93,
  output out_94,
  output out_95,
  output out_96,
  output out_97,
  output out_98,
  output out_99,
  output out_100,
  output out_101,
  output out_102,
  output out_103,
  output out_104,
  output out_105,
  output out_106,
  output out_107,
  output out_108,
  output out_109,
  output out_110,
  output out_111,
  output out_112,
  output out_113,
  output out_114,
  output out_115,
  output out_116,
  output out_117,
  output out_118,
  output out_119,
  output out_120,
  output out_121,
  output out_122,
  output out_123,
  output out_124,
  output out_125,
  output out_126,
  output out_127,
  output out_128,
  output out_129,
  output out_130
);

  d_flip_flop d_flip_flop_1 (.A(A0), .B(B0), .SEL(SEL), .CLK(CLK), .Q(Q_0), .Q_not(Q_0_not));
  d_flip_flop d_flip_flop_2 (.A(in_11), .B(in_15), .SEL(SEL), .CLK(CLK), .Q(out_75), .Q_not(out_79));
  d_flip_flop d_flip_flop_3 (.A(in_19), .B(in_23), .SEL(SEL), .CLK(CLK), .Q(out_83), .Q_not(out_87));
  d_flip_flop d_flip_flop_4 (.A(in_27), .B(in_31), .SEL(SEL), .CLK(CLK), .Q(out_91), .Q_not(out_95));
  d_flip_flop d_flip_flop_5 (.A(in_35), .B(in_39), .SEL(SEL), .CLK(CLK), .Q(out_99), .Q_not(out_103));
  d_flip_flop d_flip_flop_6 (.A(in_43), .B(in_47), .SEL(SEL), .CLK(CLK), .Q(out_107), .Q_not(out_111));
  d_flip_flop d_flip_flop_7 (.A(in_51), .B(in_55), .SEL(SEL), .CLK(CLK), .Q(out_115), .Q_not(out_119));
  d_flip_flop d_flip_flop_8 (.A(in_59), .B(in_63), .SEL(SEL), .CLK(CLK), .Q(out_123), .Q_not(out_127));
  d_flip_flop d_flip_flop_9 (.A(A1), .B(B1), .SEL(SEL), .CLK(CLK), .Q(Q_1), .Q_not(Q_1_not));
  d_flip_flop d_flip_flop_10 (.A(in_12), .B(in_16), .SEL(SEL), .CLK(CLK), .Q(out_76), .Q_not(out_80));
  d_flip_flop d_flip_flop_11 (.A(in_20), .B(in_24), .SEL(SEL), .CLK(CLK), .Q(out_84), .Q_not(out_88));
  d_flip_flop d_flip_flop_12 (.A(in_28), .B(in_32), .SEL(SEL), .CLK(CLK), .Q(out_92), .Q_not(out_96));
  d_flip_flop d_flip_flop_13 (.A(in_36), .B(in_40), .SEL(SEL), .CLK(CLK), .Q(out_100), .Q_not(out_104));
  d_flip_flop d_flip_flop_14 (.A(in_44), .B(in_48), .SEL(SEL), .CLK(CLK), .Q(out_108), .Q_not(out_112));
  d_flip_flop d_flip_flop_15 (.A(in_52), .B(in_56), .SEL(SEL), .CLK(CLK), .Q(out_116), .Q_not(out_120));
  d_flip_flop d_flip_flop_16 (.A(in_60), .B(in_64), .SEL(SEL), .CLK(CLK), .Q(out_124), .Q_not(out_128));
  d_flip_flop d_flip_flop_17 (.A(A2), .B(B2), .SEL(SEL), .CLK(CLK), .Q(Q_2), .Q_not(Q_2_not));
  d_flip_flop d_flip_flop_18 (.A(in_13), .B(in_17), .SEL(SEL), .CLK(CLK), .Q(out_77), .Q_not(out_81));
  d_flip_flop d_flip_flop_19 (.A(in_21), .B(in_25), .SEL(SEL), .CLK(CLK), .Q(out_85), .Q_not(out_89));
  d_flip_flop d_flip_flop_20 (.A(in_29), .B(in_33), .SEL(SEL), .CLK(CLK), .Q(out_93), .Q_not(out_97));
  d_flip_flop d_flip_flop_21 (.A(in_37), .B(in_41), .SEL(SEL), .CLK(CLK), .Q(out_101), .Q_not(out_105));
  d_flip_flop d_flip_flop_22 (.A(in_45), .B(in_49), .SEL(SEL), .CLK(CLK), .Q(out_109), .Q_not(out_113));
  d_flip_flop d_flip_flop_23 (.A(in_53), .B(in_57), .SEL(SEL), .CLK(CLK), .Q(out_117), .Q_not(out_121));
  d_flip_flop d_flip_flop_24 (.A(in_61), .B(in_65), .SEL(SEL), .CLK(CLK), .Q(out_125), .Q_not(out_129));
  d_flip_flop d_flip_flop_25 (.A(A3), .B(B3), .SEL(SEL), .CLK(CLK), .Q(Q_3), .Q_not(Q_3_not));
  d_flip_flop d_flip_flop_26 (.A(in_14), .B(in_18), .SEL(SEL), .CLK(CLK), .Q(out_78), .Q_not(out_82));
  d_flip_flop d_flip_flop_27 (.A(in_22), .B(in_26), .SEL(SEL), .CLK(CLK), .Q(out_86), .Q_not(out_90));
  d_flip_flop d_flip_flop_28 (.A(in_30), .B(in_34), .SEL(SEL), .CLK(CLK), .Q(out_94), .Q_not(out_98));
  d_flip_flop d_flip_flop_29 (.A(in_38), .B(in_42), .SEL(SEL), .CLK(CLK), .Q(out_102), .Q_not(out_106));
  d_flip_flop d_flip_flop_30 (.A(in_46), .B(in_50), .SEL(SEL), .CLK(CLK), .Q(out_110), .Q_not(out_114));
  d_flip_flop d_flip_flop_31 (.A(in_54), .B(in_58), .SEL(SEL), .CLK(CLK), .Q(out_118), .Q_not(out_122));
  d_flip_flop d_flip_flop_32 (.A(in_62), .B(in_66), .SEL(SEL), .CLK(CLK), .Q(out_126), .Q_not(out_130));
endmodule

module sr_latch (
  input  R,
  input  S,
  output out_3,
  output out_4
);

  nand nand_1 (out_3, R, out_4);
  nand nand_2 (out_4, out_3, S);
endmodule

module d_latch (
  input  in_1,
  input  in_2,
  output out_3,
  output out_4
);

  wire nand_1_out, nand_2_out, not_1_out;

  not not_1 (not_1_out, in_1);
  nand nand_1 (nand_1_out, in_1, in_2);
  nand nand_2 (nand_2_out, not_1_out, in_2);
  sr_latch sr_latch_1 (.R(nand_1_out), .S(nand_2_out), .out_3(out_3), .out_4(out_4));
endmodule

module d_flip_flop (
  input  A,
  input  B,
  input  SEL,
  input  CLK,
  output Q,
  output Q_not
);

  wire MASTER_out_3, mux_2_to_1_1_out_4, not_1_out;

  mux_2_to_1 mux_2_to_1_1 (.A(A), .B(B), .SEL(SEL), .out_4(mux_2_to_1_1_out_4));
  not not_1 (not_1_out, CLK);
  d_latch MASTER (.in_1(mux_2_to_1_1_out_4), .in_2(not_1_out), .out_3(MASTER_out_3));  // open: out_4
  d_latch SLAVE (.in_1(MASTER_out_3), .in_2(CLK), .out_3(Q), .out_4(Q_not));
endmodule

module mux_2_to_1 (
  input  A,
  input  B,
  input  SEL,
  output out_4
);

  wire a_and_selnot_out, b_and_sel_out, not_1_out;

  not not_1 (not_1_out, SEL);
  nand a_and_selnot (a_and_selnot_out, A, not_1_out);
  nand b_and_sel (b_and_sel_out, B, SEL);
  nand Y (out_4, a_and_selnot_out, b_and_sel_out);
endmodule

module overflow_flag (
  input  B_MSB,
  input  A_MSB,
  input  R_MSB,
  input  OP,
  output out_5
);

  wire A_XNOR_B_out, A_XOR_B_out, A_XOR_R_out, ADDITION_out, R_XOR_A_out, SUBTRACTION_out;

  xnor A_XNOR_B (A_XNOR_B_out, B_MSB, A_MSB);
  xor R_XOR_A (R_XOR_A_out, A_MSB, R_MSB);
  xor A_XOR_B (A_XOR_B_out, A_MSB, B_MSB);
  xor A_XOR_R (A_XOR_R_out, A_MSB, R_MSB);
  and ADDITION (ADDITION_out, A_XNOR_B_out, R_XOR_A_out);
  and SUBTRACTION (SUBTRACTION_out, A_XOR_B_out, A_XOR_R_out);
  mux_2_to_1 mux_2_to_1_1 (.A(ADDITION_out), .B(SUBTRACTION_out), .SEL(OP), .out_4(out_5));
endmodule

module PC_fetch (
  input  WE,
  input  CLK,
  input  RST
);

  wire [31:0] adder_1_out, PC_q;

  Register #(.width(32)) PC (.D(adder_1_out), .en(WE), .clk(CLK), .Q(PC_q), .clr(RST));
  Adder #(.width(32)) adder_1 (.a(PC_q), .b(32'h4), .out(adder_1_out), .cin(1'b0));  // open: cout
endmodule

module reg4x32file (
  input  CLK,
  input  [1:0] WA,
  input  [31:0] WD,
  input  WE,
  input  [1:0] RA,
  input  [1:0] RB,
  output [31:0] RD_A,
  output [31:0] RD_B
);

  wire and_1_out, and_2_out, and_3_out, and_4_out, decoder2x4_1_d0, decoder2x4_1_d1, decoder2x4_1_d2,
       decoder2x4_1_d3;
  wire [31:0] R0_q, R1_q, R2_q, R3_q;

  decoder2x4 decoder2x4_1 (
    .in_1(WA), .D0(decoder2x4_1_d0), .D1(decoder2x4_1_d1), .D2(decoder2x4_1_d2), .D3(decoder2x4_1_d3));
  and and_1 (and_1_out, decoder2x4_1_d0, WE);
  and and_2 (and_2_out, decoder2x4_1_d1, WE);
  and and_3 (and_3_out, decoder2x4_1_d2, WE);
  and and_4 (and_4_out, decoder2x4_1_d3, WE);
  Register #(.width(32)) R0 (.D(WD), .en(and_1_out), .clk(CLK), .Q(R0_q));  // open: clr
  Register #(.width(32)) R2 (.D(WD), .en(and_3_out), .clk(CLK), .Q(R2_q));  // open: clr
  Register #(.width(32)) R1 (.D(WD), .en(and_2_out), .clk(CLK), .Q(R1_q));  // open: clr
  Register #(.width(32)) R3 (.D(WD), .en(and_4_out), .clk(CLK), .Q(R3_q));  // open: clr
  Multiplexer #(.select(2), .width(32)) multiplexer_1 (
    .in0(R0_q), .in1(R1_q), .in2(R2_q), .in3(R3_q), .out(RD_A), .sel(RA));
  Multiplexer #(.select(2), .width(32)) multiplexer_2 (
    .in0(R0_q), .in1(R1_q), .in2(R2_q), .in3(R3_q), .out(RD_B), .sel(RB));
endmodule

module decoder2x4 (
  input  [1:0] in_1,
  output D0,
  output D1,
  output D2,
  output D3
);

  wire NOT_A0_out, NOT_A1_out;

  not NOT_A0 (NOT_A0_out, in_1[0]);
  not NOT_A1 (NOT_A1_out, in_1[1]);
  and and_1 (D0, NOT_A0_out, NOT_A1_out);
  and and_2 (D1, NOT_A1_out, in_1[0]);
  and and_3 (D2, in_1[1], NOT_A0_out);
  and and_4 (D3, in_1[1], in_1[0]);
endmodule
