// Logisim project ALU_modular_design.circ as structural Verilog
module main (
  input  A_0,
  input  A_1,
  input  A_2,
  input  A_3,
  input  B_0,
  input  B_1,
  input  B_2,
  input  A_4,
  input  SUB,
  input  SEL0,
  input  SEL1,
  input  in_12,
  input  in_13,
  input  in_14,
  input  in_15,
  input  in_16,
  input  in_17,
  input  in_18,
  input  in_19,
  input  in_20,
  input  in_21,
  input  in_22,
  input  in_23,
  input  in_24,
  input  in_25,
  input  in_26,
  input  in_27,
  input  in_28,
  input  in_29,
  input  in_30,
  input  in_31,
  input  in_32,
  input  in_33,
  input  in_34,
  input  in_35,
  input  in_36,
  input  in_37,
  input  in_38,
  input  in_39,
  input  in_40,
  input  in_41,
  input  in_42,
  input  in_43,
  input  in_44,
  input  in_45,
  input  in_46,
  input  in_47,
  input  in_48,
  input  in_49,
  input  in_50,
  input  in_51,
  input  in_52,
  input  in_53,
  input  in_54,
  input  in_55,
  input  in_56,
  input  in_57,
  input  in_58,
  input  in_59,
  input  in_60,
  input  in_61,
  input  in_62,
  input  in_63,
  input  in_64,
  input  in_65,
  input  in_66,
  input  in_67,
  output out_68,
  output out_69,
  output out_70,
  output out_71,
  output out_72,
  output out_73,
  output out_74,
  output out_75,
  output out_76,
  output out_77,
  output out_78,
  output out_79,
  output out_80,
  output out_81,
  output out_82,
  output out_83,
  output out_84,
  output out_85,
  output out_86,
  output out_87,
  output out_88,
  output out_89,
  output out_90,
  output out_91,
  output out_92,
  output out_93,
  output out_94,
  output out_95,
  output out_96,
  output out_97,
  output out_98,
  output out_99
);

  wire alu_1bit_1_cout_output, alu_1bit_2_cout_output, alu_1bit_3_cout_output, alu_1bit_4_cout_output,
       alu_1bit_5_cout_output, alu_1bit_6_cout_output, alu_1bit_7_cout_output, alu_1bit_8_cout_output,
       alu_1bit_9_cout_output, alu_1bit_10_cout_output, alu_1bit_11_cout_output, alu_1bit_12_cout_output,
       alu_1bit_13_cout_output, alu_1bit_14_cout_output, alu_1bit_15_cout_output, alu_1bit_16_cout_output,
       alu_1bit_17_cout_output, alu_1bit_18_cout_output, alu_1bit_19_cout_output, alu_1bit_20_cout_output,
       alu_1bit_21_cout_output, alu_1bit_22_cout_output, alu_1bit_23_cout_output, alu_1bit_24_cout_output,
       alu_1bit_25_cout_output, alu_1bit_26_cout_output, alu_1bit_27_cout_output, alu_1bit_28_cout_output,
       alu_1bit_29_cout_output, alu_1bit_30_cout_output, alu_1bit_31_cout_output, alu_1bit_32_cout_output,
       clock_1_out, register_1_q;
  wire [3:0] register_2_q, register_2_q_2, register_2_q_3, register_2_q_4;

  Hex_Digit_Display hex_digit_display_1 (.value({out_99, out_98, out_97, out_96}));  // open: dp
  Hex_Digit_Display hex_digit_display_2 (.value({out_95, out_94, out_93, out_92}));  // open: dp
  Hex_Digit_Display hex_digit_display_3 (.value({out_91, out_90, out_89, out_88}));  // open: dp
  Hex_Digit_Display hex_digit_display_4 (.value({out_87, out_86, out_85, out_84}));  // open: dp
  Hex_Digit_Display hex_digit_display_5 (.value(register_2_q_4));  // open: dp
  Hex_Digit_Display hex_digit_display_6 (.value(register_2_q_3));  // open: dp
  Hex_Digit_Display hex_digit_display_7 (.value(register_2_q_2));  // open: dp
  Hex_Digit_Display hex_digit_display_8 (.value(register_2_q));  // open: dp
  Register #(.width(1)) register_1 (.D(alu_1bit_32_cout_output), .clk(clock_1_out), .Q(register_1_q));  // open: en, clr
  LED led_1 (.in(register_1_q));
  Register #(.width(16)) register_2 (
    .D({out_83, out_82, out_81, out_80, out_79, out_78, out_77, out_76, out_75, out_74, out_73, out_72, out_71, out_70, out_69, out_68}),
    .clk(clock_1_out), .Q({register_2_q_4, register_2_q_3, register_2_q_2, register_2_q}));  // open: en, clr
  Clock clock_1 (.out(clock_1_out));
  ALU_1bit alu_1bit_1 (
    .A(A_0), .B(B_0), .SUB(SUB), .Cin(SUB), .SEL0(SEL0), .SEL1(SEL1), .Cout_output(alu_1bit_1_cout_output),
    .out_8(out_68));
  ALU_1bit alu_1bit_2 (
    .A(in_12), .B(in_16), .SUB(SUB), .Cin(alu_1bit_25_cout_output), .SEL0(SEL0), .SEL1(SEL1),
    .Cout_output(alu_1bit_2_cout_output), .out_8(out_72));
  ALU_1bit alu_1bit_3 (
    .A(in_20), .B(in_24), .SUB(SUB), .Cin(alu_1bit_26_cout_output), .SEL0(SEL0), .SEL1(SEL1),
    .Cout_output(alu_1bit_3_cout_output), .out_8(out_76));
  ALU_1bit alu_1bit_4 (
    .A(in_28), .B(in_32), .SUB(SUB), .Cin(alu_1bit_27_cout_output), .SEL0(SEL0), .SEL1(SEL1),
    .Cout_output(alu_1bit_4_cout_output), .out_8(out_80));
  ALU_1bit alu_1bit_5 (
    .A(in_36), .B(in_40), .SUB(SUB), .Cin(alu_1bit_28_cout_output), .SEL0(SEL0), .SEL1(SEL1),
    .Cout_output(alu_1bit_5_cout_output), .out_8(out_84));
  ALU_1bit alu_1bit_6 (
    .A(in_44), .B(in_48), .SUB(SUB), .Cin(alu_1bit_29_cout_output), .SEL0(SEL0), .SEL1(SEL1),
    .Cout_output(alu_1bit_6_cout_output), .out_8(out_88));
  ALU_1bit alu_1bit_7 (
    .A(in_52), .B(in_56), .SUB(SUB), .Cin(alu_1bit_30_cout_output), .SEL0(SEL0), .SEL1(SEL1),
    .Cout_output(alu_1bit_7_cout_output), .out_8(out_92));
  ALU_1bit alu_1bit_8 (
    .A(in_60), .B(in_64), .SUB(SUB), .Cin(alu_1bit_31_cout_output), .SEL0(SEL0), .SEL1(SEL1),
    .Cout_output(alu_1bit_8_cout_output), .out_8(out_96));
  ALU_1bit alu_1bit_9 (
    .A(A_1), .B(B_1), .SUB(SUB), .Cin(alu_1bit_1_cout_output), .SEL0(SEL0), .SEL1(SEL1),
    .Cout_output(alu_1bit_9_cout_output), .out_8(out_69));
  ALU_1bit alu_1bit_10 (
    .A(in_13), .B(in_17), .SUB(SUB), .Cin(alu_1bit_2_cout_output), .SEL0(SEL0), .SEL1(SEL1),
    .Cout_output(alu_1bit_10_cout_output), .out_8(out_73));
  ALU_1bit alu_1bit_11 (
    .A(in_21), .B(in_25), .SUB(SUB), .Cin(alu_1bit_3_cout_output), .SEL0(SEL0), .SEL1(SEL1),
    .Cout_output(alu_1bit_11_cout_output), .out_8(out_77));
  ALU_1bit alu_1bit_12 (
    .A(in_29), .B(in_33), .SUB(SUB), .Cin(alu_1bit_4_cout_output), .SEL0(SEL0), .SEL1(SEL1),
    .Cout_output(alu_1bit_12_cout_output), .out_8(out_81));
  ALU_1bit alu_1bit_13 (
    .A(in_37), .B(in_41), .SUB(SUB), .Cin(alu_1bit_5_cout_output), .SEL0(SEL0), .SEL1(SEL1),
    .Cout_output(alu_1bit_13_cout_output), .out_8(out_85));
  ALU_1bit alu_1bit_14 (
    .A(in_45), .B(in_49), .SUB(SUB), .Cin(alu_1bit_6_cout_output), .SEL0(SEL0), .SEL1(SEL1),
    .Cout_output(alu_1bit_14_cout_output), .out_8(out_89));
  ALU_1bit alu_1bit_15 (
    .A(in_53), .B(in_57), .SUB(SUB), .Cin(alu_1bit_7_cout_output), .SEL0(SEL0), .SEL1(SEL1),
    .Cout_output(alu_1bit_15_cout_output), .out_8(out_93));
  ALU_1bit alu_1bit_16 (
    .A(in_61), .B(in_65), .SUB(SUB), .Cin(alu_1bit_8_cout_output), .SEL0(SEL0), .SEL1(SEL1),
    .Cout_output(alu_1bit_16_cout_output), .out_8(out_97));
  ALU_1bit alu_1bit_17 (
    .A(A_2), .B(B_2), .SUB(SUB), .Cin(alu_1bit_9_cout_output), .SEL0(SEL0), .SEL1(SEL1),
    .Cout_output(alu_1bit_17_cout_output), .out_8(out_70));
  ALU_1bit alu_1bit_18 (
    .A(in_14), .B(in_18), .SUB(SUB), .Cin(alu_1bit_10_cout_output), .SEL0(SEL0), .SEL1(SEL1),
    .Cout_output(alu_1bit_18_cout_output), .out_8(out_74));
  ALU_1bit alu_1bit_19 (
    .A(in_22), .B(in_26), .SUB(SUB), .Cin(alu_1bit_11_cout_output), .SEL0(SEL0), .SEL1(SEL1),
    .Cout_output(alu_1bit_19_cout_output), .out_8(out_78));
  ALU_1bit alu_1bit_20 (
    .A(in_30), .B(in_34), .SUB(SUB), .Cin(alu_1bit_12_cout_output), .SEL0(SEL0), .SEL1(SEL1),
    .Cout_output(alu_1bit_20_cout_output), .out_8(out_82));
  ALU_1bit alu_1bit_21 (
    .A(in_38), .B(in_42), .SUB(SUB), .Cin(alu_1bit_13_cout_output), .SEL0(SEL0), .SEL1(SEL1),
    .Cout_output(alu_1bit_21_cout_output), .out_8(out_86));
  ALU_1bit alu_1bit_22 (
    .A(in_46), .B(in_50), .SUB(SUB), .Cin(alu_1bit_14_cout_output), .SEL0(SEL0), .SEL1(SEL1),
    .Cout_output(alu_1bit_22_cout_output), .out_8(out_90));
  ALU_1bit alu_1bit_23 (
    .A(in_54), .B(in_58), .SUB(SUB), .Cin(alu_1bit_15_cout_output), .SEL0(SEL0), .SEL1(SEL1),
    .Cout_output(alu_1bit_23_cout_output), .out_8(out_94));
  ALU_1bit alu_1bit_24 (
    .A(in_62), .B(in_66), .SUB(SUB), .Cin(alu_1bit_16_cout_output), .SEL0(SEL0), .SEL1(SEL1),
    .Cout_output(alu_1bit_24_cout_output), .out_8(out_98));
  ALU_1bit alu_1bit_25 (
    .A(A_3), .B(A_4), .SUB(SUB), .Cin(alu_1bit_17_cout_output), .SEL0(SEL0), .SEL1(SEL1),
    .Cout_output(alu_1bit_25_cout_output), .out_8(out_71));
  ALU_1bit alu_1bit_26 (
    .A(in_15), .B(in_19), .SUB(SUB), .Cin(alu_1bit_18_cout_output), .SEL0(SEL0), .SEL1(SEL1),
    .Cout_output(alu_1bit_26_cout_output), .out_8(out_75));
  ALU_1bit alu_1bit_27 (
    .A(in_23), .B(in_27), .SUB(SUB), .Cin(alu_1bit_19_cout_output), .SEL0(SEL0), .SEL1(SEL1),
    .Cout_output(alu_1bit_27_cout_output), .out_8(out_79));
  ALU_1bit alu_1bit_28 (
    .A(in_31), .B(in_35), .SUB(SUB), .Cin(alu_1bit_20_cout_output), .SEL0(SEL0), .SEL1(SEL1),
    .Cout_output(alu_1bit_28_cout_output), .out_8(out_83));
  ALU_1bit alu_1bit_29 (
    .A(in_39), .B(in_43), .SUB(SUB), .Cin(alu_1bit_21_cout_output), .SEL0(SEL0), .SEL1(SEL1),
    .Cout_output(alu_1bit_29_cout_output), .out_8(out_87));
  ALU_1bit alu_1bit_30 (
    .A(in_47), .B(in_51), .SUB(SUB), .Cin(alu_1bit_22_cout_output), .SEL0(SEL0), .SEL1(SEL1),
    .Cout_output(alu_1bit_30_cout_output), .out_8(out_91));
  ALU_1bit alu_1bit_31 (
    .A(in_55), .B(in_59), .SUB(SUB), .Cin(alu_1bit_23_cout_output), .SEL0(SEL0), .SEL1(SEL1),
    .Cout_output(alu_1bit_31_cout_output), .out_8(out_95));
  ALU_1bit alu_1bit_32 (
    .A(in_63), .B(in_67), .SUB(SUB), .Cin(alu_1bit_24_cout_output), .SEL0(SEL0), .SEL1(SEL1),
    .Cout_output(alu_1bit_32_cout_output), .out_8(out_99));

  // Notes on the sheet:
  //   CLK
endmodule

module ALU_1bit (
  input  A,
  input  B,
  input  SUB,
  input  Cin,
  input  SEL0,
  input  SEL1,
  output Cout_output,
  output out_8
);

  wire AND_out_out, Beff_out, OR_out_out, SUM_out, t1_out, t2_out, X_out, XOR_out_out;

  and AND_out (AND_out_out, A, B);
  or OR_out (OR_out_out, A, B);
  xor XOR_out (XOR_out_out, A, B);
  xor Beff (Beff_out, B, SUB);
  xor X (X_out, A, Beff_out);
  and t1 (t1_out, A, Beff_out);
  and t2 (t2_out, X_out, Cin);
  xor SUM (SUM_out, X_out, Cin);
  or Cout (Cout_output, t1_out, t2_out);
  mux_4_to_1 mux_4_to_1_1 (
    .A(AND_out_out), .B(OR_out_out), .C(SUM_out), .D(XOR_out_out), .Sel_0(SEL0), .Sel_1(SEL1), .out_7(out_8));
endmodule

module mux_4_to_1 (
  input  A,
  input  B,
  input  C,
  input  D,
  input  Sel_0,
  input  Sel_1,
  output out_7
);

  wire nand_1_out, nand_2_out, nand_3_out, nand_4_out, nand_5_out, nand_6_out;

  nand nand_1 (nand_1_out, Sel_0, Sel_0);
  nand nand_2 (nand_2_out, Sel_1, Sel_1);
  nand nand_3 (nand_3_out, A, nand_1_out, nand_2_out);
  nand nand_4 (nand_4_out, B, nand_1_out, Sel_1);
  nand nand_5 (nand_5_out, C, nand_2_out, Sel_0);
  nand nand_6 (nand_6_out, D, Sel_0, Sel_1);
  nand nand_7 (out_7, nand_3_out, nand_4_out, nand_5_out, nand_6_out);
endmodule
