// Logisim project armv4t.circ as structural Verilog: 7 circuits, main circuit main
module main (
  input  [31:0] in_1,
  input  [31:0] in_2,
  input  in_3,
  output [31:0] out_4,
  output out_5
);

  ks_32_sub ks_32_sub_1 (.in_1(in_1), .in_2(in_2), .SUB(in_3), .out_4(out_4), .out_5(out_5));
endmodule

module koggle_stone_1b (
  input  A,
  input  B,
  input  C_in,
  output g,
  output p,
  output sum
);

  and a_and_b (g, A, B);
  xor a_xor_b (p, A, B);
  xor p_xor_cin (sum, p, C_in);
endmodule

module koggle_stone_2b (
  input  A0,
  input  B0,
  input  CIN,
  input  A1,
  input  B1,
  output SUM0,
  output Cout,
  output SUM1
);

  wire bit0_g, bit0_p, bit1_g, bit1_p, pg1_g_out;

  koggle_stone_1b bit0 (.A(A0), .B(B0), .C_in(CIN), .g(bit0_g), .p(bit0_p), .sum(SUM0));
  koggle_stone_1b bit1 (.A(A1), .B(B1), .C_in(pg1_g_out), .g(bit1_g), .p(bit1_p), .sum(SUM1));
  pg_cell pg1 (.G(bit0_g), .P(bit0_p), .G_prev(CIN), .G_out(pg1_g_out));  // open: P_Prev, P_out
  pg_cell pg2 (.G(bit1_g), .P(bit1_p), .G_prev(pg1_g_out), .G_out(Cout));  // open: P_Prev, P_out
endmodule

module pg_cell (
  input  G,
  input  P,
  input  G_prev,
  input  P_Prev,
  output G_out,
  output P_out
);

  wire PandG_prev_out;

  and PandG_prev (PandG_prev_out, P, G_prev);
  and P_and_P_prev (P_out, P, P_Prev);
  or G_or_PandG_prev (G_out, G, PandG_prev_out);
endmodule

module ks_4b (
  input  in_1,
  input  in_2,
  input  in_3,
  input  in_4,
  input  in_5,
  input  in_6,
  input  in_7,
  input  in_8,
  input  in_9,
  output out_10,
  output out_11,
  output out_12,
  output out_13,
  output out_14
);

  wire bit0_g, bit0_p, bit1_g, bit1_p, bit2_g, bit2_p, koggle_stone_1b_1_g, koggle_stone_1b_1_p, s1_0_g_out,
       s1_0_p_out, s1_1_g_out, s1_1_p_out, s1_2_g_out, s1_2_p_out, s1_3_g_out, s1_3_p_out, s2_2_g_out;

  pg_cell s1_3 (
    .G(koggle_stone_1b_1_g), .P(koggle_stone_1b_1_p), .G_prev(bit2_g), .P_Prev(bit2_p), .G_out(s1_3_g_out),
    .P_out(s1_3_p_out));
  pg_cell s2_3 (
    .G(s1_3_g_out), .P(s1_3_p_out), .G_prev(s1_1_g_out), .P_Prev(s1_1_p_out), .G_out(out_14));  // open: P_out
  koggle_stone_1b koggle_stone_1b_1 (
    .A(in_1), .B(in_5), .C_in(s2_2_g_out), .g(koggle_stone_1b_1_g), .p(koggle_stone_1b_1_p), .sum(out_10));
  pg_cell s1_2 (.G(bit2_g), .P(bit2_p), .G_prev(bit1_g), .P_Prev(bit1_p), .G_out(s1_2_g_out), .P_out(s1_2_p_out));
  pg_cell s2_2 (
    .G(s1_2_g_out), .P(s1_2_p_out), .G_prev(s1_0_g_out), .P_Prev(s1_0_p_out), .G_out(s2_2_g_out));  // open: P_out
  koggle_stone_1b bit2 (.A(in_2), .B(in_6), .C_in(s1_1_g_out), .g(bit2_g), .p(bit2_p), .sum(out_11));
  pg_cell s1_1 (.G(bit1_g), .P(bit1_p), .G_prev(bit0_g), .P_Prev(bit0_p), .G_out(s1_1_g_out), .P_out(s1_1_p_out));
  koggle_stone_1b bit1 (.A(in_3), .B(in_7), .C_in(s1_0_g_out), .g(bit1_g), .p(bit1_p), .sum(out_12));
  pg_cell s1_0 (.G(bit0_g), .P(bit0_p), .G_prev(in_9), .G_out(s1_0_g_out), .P_out(s1_0_p_out));  // open: P_Prev
  koggle_stone_1b bit0 (.A(in_4), .B(in_8), .C_in(in_9), .g(bit0_g), .p(bit0_p), .sum(out_13));
endmodule

module ks_32b (
  input  [31:0] A,
  input  [31:0] B,
  input  Cin,
  output SUM31,
  output SUM30,
  output SUM29,
  output SUM28,
  output SUM27,
  output SUM26,
  output SUM25,
  output SUM24,
  output SUM23,
  output SUM22,
  output SUM21,
  output SUM20,
  output SUM19,
  output SUM18,
  output SUM17,
  output SUM16,
  output SUM15,
  output SUM14,
  output SUM13,
  output SUM12,
  output SUM11,
  output SUM10,
  output SUM9,
  output SUM8,
  output SUM7,
  output SUM6,
  output SUM5,
  output SUM4,
  output SUM3,
  output SUM2,
  output sum1,
  output sum0,
  output Cout
);

  wire bit3_g, bit3_p, bit7_g, bit7_p, bit8_g, bit8_p, bit9_g, bit9_p, bit10_g, bit10_p, bit11_g, bit11_p,
       bit12_g, bit12_p, bit13_g, bit13_p, bit14_g, bit14_p, bit15_g, bit15_p, bit16_g, bit16_p, bit17_g,
       bit17_p, bit18_g, bit18_p, bit19_g, bit19_p, bit20_g, bit20_p, bit21_g, bit21_p, bit22_g, bit22_p,
       bit23_g, bit23_p, bit24_g, bit24_p, bit25_g, bit25_p, bit26_g, bit26_p, bit27_g, bit27_p, bit28_g,
       bit28_p, bit29_g, bit29_p, bit30_g, bit30_p, bit31_g, bit31_p, koggle_stone_1b_1_g,
       koggle_stone_1b_1_p, koggle_stone_1b_2_g, koggle_stone_1b_2_p, koggle_stone_1b_3_g,
       koggle_stone_1b_3_p, koggle_stone_1b_4_g, koggle_stone_1b_4_p, koggle_stone_1b_5_g,
       koggle_stone_1b_5_p, koggle_stone_1b_6_g, koggle_stone_1b_6_p, pg_cell_1_g_out, pg_cell_1_p_out,
       pg_cell_2_g_out, pg_cell_2_p_out, pg_cell_3_g_out, pg_cell_3_p_out, pg_cell_5_g_out, pg_cell_5_p_out,
       pg_cell_6_g_out, pg_cell_6_p_out, pg_cell_7_g_out, pg_cell_7_p_out, pg_cell_8_g_out, pg_cell_8_p_out,
       pg_cell_9_g_out, pg_cell_10_g_out, pg_cell_10_p_out, pg_cell_11_g_out, pg_cell_11_p_out,
       pg_cell_12_g_out, pg_cell_12_p_out, pg_cell_13_g_out, pg_cell_13_p_out, pg_cell_14_g_out,
       pg_cell_15_g_out, pg_cell_15_p_out, pg_cell_16_g_out, pg_cell_16_p_out, pg_cell_17_g_out,
       pg_cell_17_p_out, pg_cell_18_g_out, pg_cell_19_g_out, pg_cell_19_p_out, pg_cell_20_g_out,
       pg_cell_20_p_out, pg_cell_21_g_out, pg_cell_21_p_out, pg_cell_22_g_out, pg_cell_22_p_out,
       pg_cell_23_g_out, pg_cell_24_g_out, pg_cell_24_p_out, pg_cell_25_g_out, pg_cell_25_p_out,
       pg_cell_26_g_out, pg_cell_26_p_out, pg_cell_27_g_out, pg_cell_27_p_out, pg_cell_28_g_out,
       pg_cell_29_g_out, pg_cell_29_p_out, pg_cell_30_g_out, pg_cell_30_p_out, pg_cell_31_g_out,
       pg_cell_31_p_out, pg_cell_32_g_out, pg_cell_32_p_out, pg_cell_33_g_out, pg_cell_34_g_out,
       pg_cell_34_p_out, pg_cell_35_g_out, pg_cell_35_p_out, pg_cell_36_g_out, pg_cell_36_p_out,
       pg_cell_37_g_out, pg_cell_38_g_out, pg_cell_38_p_out, pg_cell_39_g_out, pg_cell_39_p_out,
       pg_cell_40_g_out, pg_cell_40_p_out, pg_cell_41_g_out, pg_cell_41_p_out, pg_cell_42_g_out,
       pg_cell_42_p_out, pg_cell_43_g_out, pg_cell_43_p_out, pg_cell_44_g_out, pg_cell_44_p_out,
       pg_cell_45_g_out, pg_cell_45_p_out, pg_cell_46_g_out, pg_cell_46_p_out, pg_cell_47_g_out,
       pg_cell_47_p_out, pg_cell_48_g_out, pg_cell_48_p_out, pg_cell_49_g_out, pg_cell_49_p_out,
       pg_cell_50_g_out, pg_cell_50_p_out, pg_cell_51_g_out, pg_cell_51_p_out, pg_cell_52_g_out,
       pg_cell_52_p_out, pg_cell_53_g_out, pg_cell_53_p_out, pg_cell_54_g_out, pg_cell_54_p_out,
       pg_cell_55_g_out, pg_cell_55_p_out, pg_cell_56_g_out, pg_cell_56_p_out, pg_cell_57_g_out,
       pg_cell_57_p_out, pg_cell_58_g_out, pg_cell_58_p_out, pg_cell_59_g_out, pg_cell_59_p_out,
       pg_cell_60_g_out, pg_cell_60_p_out, pg_cell_61_g_out, pg_cell_61_p_out, pg_cell_62_g_out,
       pg_cell_62_p_out, pg_cell_63_g_out, pg_cell_63_p_out, pg_cell_64_g_out, pg_cell_64_p_out,
       pg_cell_65_g_out, pg_cell_65_p_out, pg_cell_66_g_out, pg_cell_66_p_out, pg_cell_67_g_out,
       pg_cell_67_p_out, pg_cell_68_g_out, pg_cell_68_p_out, pg_cell_69_g_out, pg_cell_69_p_out,
       pg_cell_70_g_out, pg_cell_70_p_out, pg_cell_71_g_out, pg_cell_71_p_out, pg_cell_72_g_out,
       pg_cell_72_p_out, pg_cell_73_g_out, pg_cell_73_p_out, pg_cell_74_g_out, pg_cell_74_p_out,
       pg_cell_75_g_out, pg_cell_75_p_out, pg_cell_76_g_out, pg_cell_76_p_out, pg_cell_77_g_out,
       pg_cell_77_p_out, pg_cell_78_g_out, pg_cell_78_p_out, pg_cell_79_g_out, pg_cell_79_p_out,
       pg_cell_80_g_out, pg_cell_80_p_out, pg_cell_81_g_out, pg_cell_81_p_out, pg_cell_82_g_out,
       pg_cell_82_p_out, pg_cell_83_g_out, pg_cell_83_p_out, pg_cell_84_g_out, pg_cell_84_p_out,
       pg_cell_85_g_out, pg_cell_85_p_out, pg_cell_86_g_out, pg_cell_86_p_out, pg_cell_87_g_out,
       pg_cell_87_p_out, pg_cell_88_g_out, pg_cell_88_p_out, pg_cell_89_g_out, pg_cell_89_p_out,
       pg_cell_90_g_out, pg_cell_90_p_out, pg_cell_91_g_out, pg_cell_91_p_out, pg_cell_92_g_out,
       pg_cell_92_p_out, pg_cell_93_g_out, pg_cell_93_p_out, pg_cell_94_g_out, pg_cell_94_p_out,
       pg_cell_95_g_out, pg_cell_95_p_out, pg_cell_96_g_out, pg_cell_96_p_out, pg_cell_97_g_out,
       pg_cell_97_p_out, pg_cell_98_g_out, pg_cell_98_p_out, pg_cell_99_g_out, pg_cell_99_p_out,
       pg_cell_100_g_out, pg_cell_100_p_out, pg_cell_101_g_out, pg_cell_101_p_out, pg_cell_102_g_out,
       pg_cell_102_p_out, pg_cell_103_g_out, pg_cell_103_p_out, pg_cell_104_g_out, pg_cell_104_p_out,
       pg_cell_105_g_out, pg_cell_105_p_out, pg_cell_106_g_out, pg_cell_106_p_out, pg_cell_107_g_out,
       pg_cell_107_p_out, pg_cell_108_g_out, pg_cell_108_p_out, pg_cell_109_g_out, pg_cell_109_p_out,
       pg_cell_110_g_out, pg_cell_110_p_out, pg_cell_111_g_out, pg_cell_111_p_out, pg_cell_112_g_out,
       pg_cell_112_p_out, pg_cell_113_g_out, pg_cell_113_p_out, pg_cell_114_g_out, pg_cell_114_p_out,
       s1_7_g_out, s1_7_p_out, s2_7_g_out, s2_7_p_out, s3_7_g_out, s3_7_p_out, s3_20_g_out, s3_20_p_out,
       s3_24_g_out, s3_24_p_out, s3_28_g_out, s3_28_p_out, s3_31_g_out, s3_31_p_out, s4_15_g_out,
       s4_15_p_out, s5_16_g_out, s5_17_g_out, s5_18_g_out, s5_19_g_out, s5_20_g_out, s5_21_g_out,
       s5_22_g_out, s5_23_g_out;

  koggle_stone_1b bit31 (.A(A[31]), .B(B[31]), .C_in(pg_cell_9_g_out), .g(bit31_g), .p(bit31_p), .sum(SUM31));
  pg_cell pg_cell_1 (
    .G(bit31_g), .P(bit31_p), .G_prev(bit30_g), .P_Prev(bit30_p), .G_out(pg_cell_1_g_out),
    .P_out(pg_cell_1_p_out));
  pg_cell pg_cell_2 (
    .G(pg_cell_1_g_out), .P(pg_cell_1_p_out), .G_prev(pg_cell_10_g_out), .P_Prev(pg_cell_10_p_out),
    .G_out(pg_cell_2_g_out), .P_out(pg_cell_2_p_out));
  pg_cell s3_31 (
    .G(pg_cell_2_g_out), .P(pg_cell_2_p_out), .G_prev(pg_cell_20_g_out), .P_Prev(pg_cell_20_p_out),
    .G_out(s3_31_g_out), .P_out(s3_31_p_out));
  pg_cell pg_cell_3 (
    .G(s3_31_g_out), .P(s3_31_p_out), .G_prev(pg_cell_40_g_out), .P_Prev(pg_cell_40_p_out),
    .G_out(pg_cell_3_g_out), .P_out(pg_cell_3_p_out));
  pg_cell pg_cell_4 (
    .G(pg_cell_3_g_out), .P(pg_cell_3_p_out), .G_prev(s4_15_g_out), .P_Prev(s4_15_p_out), .G_out(Cout));  // open: P_out
  koggle_stone_1b bit30 (.A(A[30]), .B(B[30]), .C_in(pg_cell_14_g_out), .g(bit30_g), .p(bit30_p), .sum(SUM30));
  pg_cell pg_cell_5 (
    .G(bit30_g), .P(bit30_p), .G_prev(bit29_g), .P_Prev(bit29_p), .G_out(pg_cell_5_g_out),
    .P_out(pg_cell_5_p_out));
  pg_cell pg_cell_6 (
    .G(pg_cell_5_g_out), .P(pg_cell_5_p_out), .G_prev(pg_cell_15_g_out), .P_Prev(pg_cell_15_p_out),
    .G_out(pg_cell_6_g_out), .P_out(pg_cell_6_p_out));
  pg_cell pg_cell_7 (
    .G(pg_cell_6_g_out), .P(pg_cell_6_p_out), .G_prev(pg_cell_25_g_out), .P_Prev(pg_cell_25_p_out),
    .G_out(pg_cell_7_g_out), .P_out(pg_cell_7_p_out));
  pg_cell pg_cell_8 (
    .G(pg_cell_7_g_out), .P(pg_cell_7_p_out), .G_prev(pg_cell_44_g_out), .P_Prev(pg_cell_44_p_out),
    .G_out(pg_cell_8_g_out), .P_out(pg_cell_8_p_out));
  pg_cell pg_cell_9 (
    .G(pg_cell_8_g_out), .P(pg_cell_8_p_out), .G_prev(pg_cell_75_g_out), .P_Prev(pg_cell_75_p_out),
    .G_out(pg_cell_9_g_out));  // open: P_out
  koggle_stone_1b bit29 (.A(A[29]), .B(B[29]), .C_in(pg_cell_18_g_out), .g(bit29_g), .p(bit29_p), .sum(SUM29));
  pg_cell pg_cell_10 (
    .G(bit29_g), .P(bit29_p), .G_prev(bit28_g), .P_Prev(bit28_p), .G_out(pg_cell_10_g_out),
    .P_out(pg_cell_10_p_out));
  pg_cell pg_cell_11 (
    .G(pg_cell_10_g_out), .P(pg_cell_10_p_out), .G_prev(pg_cell_19_g_out), .P_Prev(pg_cell_19_p_out),
    .G_out(pg_cell_11_g_out), .P_out(pg_cell_11_p_out));
  pg_cell pg_cell_12 (
    .G(pg_cell_11_g_out), .P(pg_cell_11_p_out), .G_prev(pg_cell_25_g_out), .P_Prev(pg_cell_25_p_out),
    .G_out(pg_cell_12_g_out), .P_out(pg_cell_12_p_out));
  pg_cell pg_cell_13 (
    .G(pg_cell_12_g_out), .P(pg_cell_12_p_out), .G_prev(pg_cell_48_g_out), .P_Prev(pg_cell_48_p_out),
    .G_out(pg_cell_13_g_out), .P_out(pg_cell_13_p_out));
  pg_cell pg_cell_14 (
    .G(pg_cell_13_g_out), .P(pg_cell_13_p_out), .G_prev(pg_cell_79_g_out), .P_Prev(pg_cell_79_p_out),
    .G_out(pg_cell_14_g_out));  // open: P_out
  koggle_stone_1b bit28 (.A(A[28]), .B(B[28]), .C_in(pg_cell_23_g_out), .g(bit28_g), .p(bit28_p), .sum(SUM28));
  pg_cell pg_cell_15 (
    .G(bit28_g), .P(bit28_p), .G_prev(bit27_g), .P_Prev(bit27_p), .G_out(pg_cell_15_g_out),
    .P_out(pg_cell_15_p_out));
  pg_cell pg_cell_16 (
    .G(pg_cell_15_g_out), .P(pg_cell_15_p_out), .G_prev(pg_cell_24_g_out), .P_Prev(pg_cell_24_p_out),
    .G_out(pg_cell_16_g_out), .P_out(pg_cell_16_p_out));
  pg_cell s3_28 (
    .G(pg_cell_16_g_out), .P(pg_cell_16_p_out), .G_prev(pg_cell_35_g_out), .P_Prev(pg_cell_35_p_out),
    .G_out(s3_28_g_out), .P_out(s3_28_p_out));
  pg_cell pg_cell_17 (
    .G(s3_28_g_out), .P(s3_28_p_out), .G_prev(s3_20_g_out), .P_Prev(s3_20_p_out), .G_out(pg_cell_17_g_out),
    .P_out(pg_cell_17_p_out));
  pg_cell pg_cell_18 (
    .G(pg_cell_17_g_out), .P(pg_cell_17_p_out), .G_prev(pg_cell_83_g_out), .P_Prev(pg_cell_83_p_out),
    .G_out(pg_cell_18_g_out));  // open: P_out
  koggle_stone_1b bit27 (.A(A[27]), .B(B[27]), .C_in(pg_cell_28_g_out), .g(bit27_g), .p(bit27_p), .sum(SUM27));
  pg_cell pg_cell_19 (
    .G(bit27_g), .P(bit27_p), .G_prev(bit26_g), .P_Prev(bit26_p), .G_out(pg_cell_19_g_out),
    .P_out(pg_cell_19_p_out));
  pg_cell pg_cell_20 (
    .G(pg_cell_19_g_out), .P(pg_cell_19_p_out), .G_prev(pg_cell_29_g_out), .P_Prev(pg_cell_29_p_out),
    .G_out(pg_cell_20_g_out), .P_out(pg_cell_20_p_out));
  pg_cell pg_cell_21 (
    .G(pg_cell_20_g_out), .P(pg_cell_20_p_out), .G_prev(pg_cell_39_g_out), .P_Prev(pg_cell_39_p_out),
    .G_out(pg_cell_21_g_out), .P_out(pg_cell_21_p_out));
  pg_cell pg_cell_22 (
    .G(pg_cell_21_g_out), .P(pg_cell_21_p_out), .G_prev(pg_cell_55_g_out), .P_Prev(pg_cell_55_p_out),
    .G_out(pg_cell_22_g_out), .P_out(pg_cell_22_p_out));
  pg_cell pg_cell_23 (
    .G(pg_cell_22_g_out), .P(pg_cell_22_p_out), .G_prev(pg_cell_87_g_out), .P_Prev(pg_cell_87_p_out),
    .G_out(pg_cell_23_g_out));  // open: P_out
  koggle_stone_1b bit26 (.A(A[26]), .B(B[26]), .C_in(pg_cell_33_g_out), .g(bit26_g), .p(bit26_p), .sum(SUM26));
  pg_cell pg_cell_24 (
    .G(bit26_g), .P(bit26_p), .G_prev(bit25_g), .P_Prev(bit25_p), .G_out(pg_cell_24_g_out),
    .P_out(pg_cell_24_p_out));
  pg_cell pg_cell_25 (
    .G(pg_cell_24_g_out), .P(pg_cell_24_p_out), .G_prev(pg_cell_34_g_out), .P_Prev(pg_cell_34_p_out),
    .G_out(pg_cell_25_g_out), .P_out(pg_cell_25_p_out));
  pg_cell pg_cell_26 (
    .G(pg_cell_25_g_out), .P(pg_cell_25_p_out), .G_prev(pg_cell_43_g_out), .P_Prev(pg_cell_43_p_out),
    .G_out(pg_cell_26_g_out), .P_out(pg_cell_26_p_out));
  pg_cell pg_cell_27 (
    .G(pg_cell_26_g_out), .P(pg_cell_26_p_out), .G_prev(pg_cell_59_g_out), .P_Prev(pg_cell_59_p_out),
    .G_out(pg_cell_27_g_out), .P_out(pg_cell_27_p_out));
  pg_cell pg_cell_28 (
    .G(pg_cell_27_g_out), .P(pg_cell_27_p_out), .G_prev(pg_cell_91_g_out), .P_Prev(pg_cell_91_p_out),
    .G_out(pg_cell_28_g_out));  // open: P_out
  koggle_stone_1b bit25 (.A(A[25]), .B(B[25]), .C_in(pg_cell_37_g_out), .g(bit25_g), .p(bit25_p), .sum(SUM25));
  pg_cell pg_cell_29 (
    .G(bit25_g), .P(bit25_p), .G_prev(bit24_g), .P_Prev(bit24_p), .G_out(pg_cell_29_g_out),
    .P_out(pg_cell_29_p_out));
  pg_cell pg_cell_30 (
    .G(pg_cell_29_g_out), .P(pg_cell_29_p_out), .G_prev(pg_cell_38_g_out), .P_Prev(pg_cell_38_p_out),
    .G_out(pg_cell_30_g_out), .P_out(pg_cell_30_p_out));
  pg_cell pg_cell_31 (
    .G(pg_cell_30_g_out), .P(pg_cell_30_p_out), .G_prev(pg_cell_47_g_out), .P_Prev(pg_cell_47_p_out),
    .G_out(pg_cell_31_g_out), .P_out(pg_cell_31_p_out));
  pg_cell pg_cell_32 (
    .G(pg_cell_31_g_out), .P(pg_cell_31_p_out), .G_prev(pg_cell_63_g_out), .P_Prev(pg_cell_63_p_out),
    .G_out(pg_cell_32_g_out), .P_out(pg_cell_32_p_out));
  pg_cell pg_cell_33 (
    .G(pg_cell_32_g_out), .P(pg_cell_32_p_out), .G_prev(pg_cell_95_g_out), .P_Prev(pg_cell_95_p_out),
    .G_out(pg_cell_33_g_out));  // open: P_out
  koggle_stone_1b bit24 (.A(A[24]), .B(B[24]), .C_in(s5_23_g_out), .g(bit24_g), .p(bit24_p), .sum(SUM24));
  pg_cell pg_cell_34 (
    .G(bit24_g), .P(bit24_p), .G_prev(bit23_g), .P_Prev(bit23_p), .G_out(pg_cell_34_g_out),
    .P_out(pg_cell_34_p_out));
  pg_cell pg_cell_35 (
    .G(pg_cell_34_g_out), .P(pg_cell_34_p_out), .G_prev(pg_cell_42_g_out), .P_Prev(pg_cell_42_p_out),
    .G_out(pg_cell_35_g_out), .P_out(pg_cell_35_p_out));
  pg_cell s3_24 (
    .G(pg_cell_35_g_out), .P(pg_cell_35_p_out), .G_prev(pg_cell_51_g_out), .P_Prev(pg_cell_51_p_out),
    .G_out(s3_24_g_out), .P_out(s3_24_p_out));
  pg_cell pg_cell_36 (
    .G(s3_24_g_out), .P(s3_24_p_out), .G_prev(pg_cell_67_g_out), .P_Prev(pg_cell_67_p_out),
    .G_out(pg_cell_36_g_out), .P_out(pg_cell_36_p_out));
  pg_cell pg_cell_37 (
    .G(pg_cell_36_g_out), .P(pg_cell_36_p_out), .G_prev(pg_cell_99_g_out), .P_Prev(pg_cell_99_p_out),
    .G_out(pg_cell_37_g_out));  // open: P_out
  koggle_stone_1b bit23 (.A(A[23]), .B(B[23]), .C_in(s5_22_g_out), .g(bit23_g), .p(bit23_p), .sum(SUM23));
  pg_cell pg_cell_38 (
    .G(bit23_g), .P(bit23_p), .G_prev(bit22_g), .P_Prev(bit22_p), .G_out(pg_cell_38_g_out),
    .P_out(pg_cell_38_p_out));
  pg_cell pg_cell_39 (
    .G(pg_cell_38_g_out), .P(pg_cell_38_p_out), .G_prev(pg_cell_46_g_out), .P_Prev(pg_cell_46_p_out),
    .G_out(pg_cell_39_g_out), .P_out(pg_cell_39_p_out));
  pg_cell pg_cell_40 (
    .G(pg_cell_39_g_out), .P(pg_cell_39_p_out), .G_prev(pg_cell_54_g_out), .P_Prev(pg_cell_54_p_out),
    .G_out(pg_cell_40_g_out), .P_out(pg_cell_40_p_out));
  pg_cell pg_cell_41 (
    .G(pg_cell_40_g_out), .P(pg_cell_40_p_out), .G_prev(pg_cell_71_g_out), .P_Prev(pg_cell_71_p_out),
    .G_out(pg_cell_41_g_out), .P_out(pg_cell_41_p_out));
  pg_cell s5_23 (
    .G(pg_cell_41_g_out), .P(pg_cell_41_p_out), .G_prev(s3_7_g_out), .P_Prev(s3_7_p_out), .G_out(s5_23_g_out));  // open: P_out
  koggle_stone_1b bit22 (.A(A[22]), .B(B[22]), .C_in(s5_21_g_out), .g(bit22_g), .p(bit22_p), .sum(SUM22));
  pg_cell pg_cell_42 (
    .G(bit22_g), .P(bit22_p), .G_prev(bit21_g), .P_Prev(bit21_p), .G_out(pg_cell_42_g_out),
    .P_out(pg_cell_42_p_out));
  pg_cell pg_cell_43 (
    .G(pg_cell_42_g_out), .P(pg_cell_42_p_out), .G_prev(pg_cell_50_g_out), .P_Prev(pg_cell_50_p_out),
    .G_out(pg_cell_43_g_out), .P_out(pg_cell_43_p_out));
  pg_cell pg_cell_44 (
    .G(pg_cell_43_g_out), .P(pg_cell_43_p_out), .G_prev(pg_cell_58_g_out), .P_Prev(pg_cell_58_p_out),
    .G_out(pg_cell_44_g_out), .P_out(pg_cell_44_p_out));
  pg_cell pg_cell_45 (
    .G(pg_cell_44_g_out), .P(pg_cell_44_p_out), .G_prev(pg_cell_74_g_out), .P_Prev(pg_cell_74_p_out),
    .G_out(pg_cell_45_g_out), .P_out(pg_cell_45_p_out));
  pg_cell s5_22 (
    .G(pg_cell_45_g_out), .P(pg_cell_45_p_out), .G_prev(pg_cell_102_g_out), .P_Prev(pg_cell_102_p_out),
    .G_out(s5_22_g_out));  // open: P_out
  koggle_stone_1b bit21 (.A(A[21]), .B(B[21]), .C_in(s5_20_g_out), .g(bit21_g), .p(bit21_p), .sum(SUM21));
  pg_cell pg_cell_46 (
    .G(bit21_g), .P(bit21_p), .G_prev(bit20_g), .P_Prev(bit20_p), .G_out(pg_cell_46_g_out),
    .P_out(pg_cell_46_p_out));
  pg_cell pg_cell_47 (
    .G(pg_cell_46_g_out), .P(pg_cell_46_p_out), .G_prev(pg_cell_53_g_out), .P_Prev(pg_cell_53_p_out),
    .G_out(pg_cell_47_g_out), .P_out(pg_cell_47_p_out));
  pg_cell pg_cell_48 (
    .G(pg_cell_47_g_out), .P(pg_cell_47_p_out), .G_prev(pg_cell_62_g_out), .P_Prev(pg_cell_62_p_out),
    .G_out(pg_cell_48_g_out), .P_out(pg_cell_48_p_out));
  pg_cell pg_cell_49 (
    .G(pg_cell_48_g_out), .P(pg_cell_48_p_out), .G_prev(pg_cell_78_g_out), .P_Prev(pg_cell_78_p_out),
    .G_out(pg_cell_49_g_out), .P_out(pg_cell_49_p_out));
  pg_cell s5_21 (
    .G(pg_cell_49_g_out), .P(pg_cell_49_p_out), .G_prev(pg_cell_105_g_out), .P_Prev(pg_cell_105_p_out),
    .G_out(s5_21_g_out));  // open: P_out
  koggle_stone_1b bit20 (.A(A[20]), .B(B[20]), .C_in(s5_19_g_out), .g(bit20_g), .p(bit20_p), .sum(SUM20));
  pg_cell pg_cell_50 (
    .G(bit20_g), .P(bit20_p), .G_prev(bit19_g), .P_Prev(bit19_p), .G_out(pg_cell_50_g_out),
    .P_out(pg_cell_50_p_out));
  pg_cell pg_cell_51 (
    .G(pg_cell_50_g_out), .P(pg_cell_50_p_out), .G_prev(pg_cell_57_g_out), .P_Prev(pg_cell_57_p_out),
    .G_out(pg_cell_51_g_out), .P_out(pg_cell_51_p_out));
  pg_cell s3_20 (
    .G(pg_cell_51_g_out), .P(pg_cell_51_p_out), .G_prev(pg_cell_66_g_out), .P_Prev(pg_cell_66_p_out),
    .G_out(s3_20_g_out), .P_out(s3_20_p_out));
  pg_cell pg_cell_52 (
    .G(s3_20_g_out), .P(s3_20_p_out), .G_prev(pg_cell_82_g_out), .P_Prev(pg_cell_82_p_out),
    .G_out(pg_cell_52_g_out), .P_out(pg_cell_52_p_out));
  pg_cell s5_20 (
    .G(pg_cell_52_g_out), .P(pg_cell_52_p_out), .G_prev(pg_cell_108_g_out), .P_Prev(pg_cell_108_p_out),
    .G_out(s5_20_g_out));  // open: P_out
  koggle_stone_1b bit19 (.A(A[19]), .B(B[19]), .C_in(s5_18_g_out), .g(bit19_g), .p(bit19_p), .sum(SUM19));
  pg_cell pg_cell_53 (
    .G(bit19_g), .P(bit19_p), .G_prev(bit18_g), .P_Prev(bit18_p), .G_out(pg_cell_53_g_out),
    .P_out(pg_cell_53_p_out));
  pg_cell pg_cell_54 (
    .G(pg_cell_53_g_out), .P(pg_cell_53_p_out), .G_prev(pg_cell_61_g_out), .P_Prev(pg_cell_61_p_out),
    .G_out(pg_cell_54_g_out), .P_out(pg_cell_54_p_out));
  pg_cell pg_cell_55 (
    .G(pg_cell_54_g_out), .P(pg_cell_54_p_out), .G_prev(pg_cell_70_g_out), .P_Prev(pg_cell_70_p_out),
    .G_out(pg_cell_55_g_out), .P_out(pg_cell_55_p_out));
  pg_cell pg_cell_56 (
    .G(pg_cell_55_g_out), .P(pg_cell_55_p_out), .G_prev(pg_cell_86_g_out), .P_Prev(pg_cell_86_p_out),
    .G_out(pg_cell_56_g_out), .P_out(pg_cell_56_p_out));
  pg_cell s5_19 (
    .G(pg_cell_56_g_out), .P(pg_cell_56_p_out), .G_prev(pg_cell_110_g_out), .P_Prev(pg_cell_110_p_out),
    .G_out(s5_19_g_out));  // open: P_out
  koggle_stone_1b bit18 (.A(A[18]), .B(B[18]), .C_in(s5_17_g_out), .g(bit18_g), .p(bit18_p), .sum(SUM18));
  pg_cell pg_cell_57 (
    .G(bit18_g), .P(bit18_p), .G_prev(bit17_g), .P_Prev(bit17_p), .G_out(pg_cell_57_g_out),
    .P_out(pg_cell_57_p_out));
  pg_cell pg_cell_58 (
    .G(pg_cell_57_g_out), .P(pg_cell_57_p_out), .G_prev(pg_cell_65_g_out), .P_Prev(pg_cell_65_p_out),
    .G_out(pg_cell_58_g_out), .P_out(pg_cell_58_p_out));
  pg_cell pg_cell_59 (
    .G(pg_cell_58_g_out), .P(pg_cell_58_p_out), .G_prev(pg_cell_73_g_out), .P_Prev(pg_cell_73_p_out),
    .G_out(pg_cell_59_g_out), .P_out(pg_cell_59_p_out));
  pg_cell pg_cell_60 (
    .G(pg_cell_59_g_out), .P(pg_cell_59_p_out), .G_prev(pg_cell_90_g_out), .P_Prev(pg_cell_90_p_out),
    .G_out(pg_cell_60_g_out), .P_out(pg_cell_60_p_out));
  pg_cell s5_18 (
    .G(pg_cell_60_g_out), .P(pg_cell_60_p_out), .G_prev(pg_cell_112_g_out), .P_Prev(pg_cell_112_p_out),
    .G_out(s5_18_g_out));  // open: P_out
  koggle_stone_1b bit17 (.A(A[17]), .B(B[17]), .C_in(s5_16_g_out), .g(bit17_g), .p(bit17_p), .sum(SUM17));
  pg_cell pg_cell_61 (
    .G(bit17_g), .P(bit17_p), .G_prev(bit16_g), .P_Prev(bit16_p), .G_out(pg_cell_61_g_out),
    .P_out(pg_cell_61_p_out));
  pg_cell pg_cell_62 (
    .G(pg_cell_61_g_out), .P(pg_cell_61_p_out), .G_prev(pg_cell_69_g_out), .P_Prev(pg_cell_69_p_out),
    .G_out(pg_cell_62_g_out), .P_out(pg_cell_62_p_out));
  pg_cell pg_cell_63 (
    .G(pg_cell_62_g_out), .P(pg_cell_62_p_out), .G_prev(pg_cell_77_g_out), .P_Prev(pg_cell_77_p_out),
    .G_out(pg_cell_63_g_out), .P_out(pg_cell_63_p_out));
  pg_cell pg_cell_64 (
    .G(pg_cell_63_g_out), .P(pg_cell_63_p_out), .G_prev(pg_cell_94_g_out), .P_Prev(pg_cell_94_p_out),
    .G_out(pg_cell_64_g_out), .P_out(pg_cell_64_p_out));
  pg_cell s5_17 (
    .G(pg_cell_64_g_out), .P(pg_cell_64_p_out), .G_prev(pg_cell_113_g_out), .P_Prev(pg_cell_113_p_out),
    .G_out(s5_17_g_out));  // open: P_out
  koggle_stone_1b bit16 (.A(A[16]), .B(B[16]), .C_in(s4_15_g_out), .g(bit16_g), .p(bit16_p), .sum(SUM16));
  pg_cell pg_cell_65 (
    .G(bit16_g), .P(bit16_p), .G_prev(bit15_g), .P_Prev(bit15_p), .G_out(pg_cell_65_g_out),
    .P_out(pg_cell_65_p_out));
  pg_cell pg_cell_66 (
    .G(pg_cell_65_g_out), .P(pg_cell_65_p_out), .G_prev(pg_cell_72_g_out), .P_Prev(pg_cell_72_p_out),
    .G_out(pg_cell_66_g_out), .P_out(pg_cell_66_p_out));
  pg_cell pg_cell_67 (
    .G(pg_cell_66_g_out), .P(pg_cell_66_p_out), .G_prev(pg_cell_81_g_out), .P_Prev(pg_cell_81_p_out),
    .G_out(pg_cell_67_g_out), .P_out(pg_cell_67_p_out));
  pg_cell pg_cell_68 (
    .G(pg_cell_67_g_out), .P(pg_cell_67_p_out), .G_prev(pg_cell_98_g_out), .P_Prev(pg_cell_98_p_out),
    .G_out(pg_cell_68_g_out), .P_out(pg_cell_68_p_out));
  pg_cell s5_16 (
    .G(pg_cell_68_g_out), .P(pg_cell_68_p_out), .G_prev(pg_cell_114_g_out), .P_Prev(pg_cell_114_p_out),
    .G_out(s5_16_g_out));  // open: P_out
  koggle_stone_1b bit15 (.A(A[15]), .B(B[15]), .C_in(pg_cell_75_g_out), .g(bit15_g), .p(bit15_p), .sum(SUM15));
  pg_cell pg_cell_69 (
    .G(bit15_g), .P(bit15_p), .G_prev(bit14_g), .P_Prev(bit14_p), .G_out(pg_cell_69_g_out),
    .P_out(pg_cell_69_p_out));
  pg_cell pg_cell_70 (
    .G(pg_cell_69_g_out), .P(pg_cell_69_p_out), .G_prev(pg_cell_76_g_out), .P_Prev(pg_cell_76_p_out),
    .G_out(pg_cell_70_g_out), .P_out(pg_cell_70_p_out));
  pg_cell pg_cell_71 (
    .G(pg_cell_70_g_out), .P(pg_cell_70_p_out), .G_prev(pg_cell_85_g_out), .P_Prev(pg_cell_85_p_out),
    .G_out(pg_cell_71_g_out), .P_out(pg_cell_71_p_out));
  pg_cell s4_15 (
    .G(pg_cell_71_g_out), .P(pg_cell_71_p_out), .G_prev(s3_7_g_out), .P_Prev(s3_7_p_out),
    .G_out(s4_15_g_out), .P_out(s4_15_p_out));
  koggle_stone_1b bit14 (.A(A[14]), .B(B[14]), .C_in(pg_cell_79_g_out), .g(bit14_g), .p(bit14_p), .sum(SUM14));
  pg_cell pg_cell_72 (
    .G(bit14_g), .P(bit14_p), .G_prev(bit13_g), .P_Prev(bit13_p), .G_out(pg_cell_72_g_out),
    .P_out(pg_cell_72_p_out));
  pg_cell pg_cell_73 (
    .G(pg_cell_72_g_out), .P(pg_cell_72_p_out), .G_prev(pg_cell_80_g_out), .P_Prev(pg_cell_80_p_out),
    .G_out(pg_cell_73_g_out), .P_out(pg_cell_73_p_out));
  pg_cell pg_cell_74 (
    .G(pg_cell_73_g_out), .P(pg_cell_73_p_out), .G_prev(pg_cell_89_g_out), .P_Prev(pg_cell_89_p_out),
    .G_out(pg_cell_74_g_out), .P_out(pg_cell_74_p_out));
  pg_cell pg_cell_75 (
    .G(pg_cell_74_g_out), .P(pg_cell_74_p_out), .G_prev(pg_cell_102_g_out), .P_Prev(pg_cell_102_p_out),
    .G_out(pg_cell_75_g_out), .P_out(pg_cell_75_p_out));
  koggle_stone_1b bit13 (.A(A[13]), .B(B[13]), .C_in(pg_cell_83_g_out), .g(bit13_g), .p(bit13_p), .sum(SUM13));
  pg_cell pg_cell_76 (
    .G(bit13_g), .P(bit13_p), .G_prev(bit12_g), .P_Prev(bit12_p), .G_out(pg_cell_76_g_out),
    .P_out(pg_cell_76_p_out));
  pg_cell pg_cell_77 (
    .G(pg_cell_76_g_out), .P(pg_cell_76_p_out), .G_prev(pg_cell_84_g_out), .P_Prev(pg_cell_84_p_out),
    .G_out(pg_cell_77_g_out), .P_out(pg_cell_77_p_out));
  pg_cell pg_cell_78 (
    .G(pg_cell_77_g_out), .P(pg_cell_77_p_out), .G_prev(pg_cell_93_g_out), .P_Prev(pg_cell_93_p_out),
    .G_out(pg_cell_78_g_out), .P_out(pg_cell_78_p_out));
  pg_cell pg_cell_79 (
    .G(pg_cell_78_g_out), .P(pg_cell_78_p_out), .G_prev(pg_cell_105_g_out), .P_Prev(pg_cell_105_p_out),
    .G_out(pg_cell_79_g_out), .P_out(pg_cell_79_p_out));
  koggle_stone_1b bit12 (.A(A[12]), .B(B[12]), .C_in(pg_cell_87_g_out), .g(bit12_g), .p(bit12_p), .sum(SUM12));
  pg_cell pg_cell_80 (
    .G(bit12_g), .P(bit12_p), .G_prev(bit11_g), .P_Prev(bit11_p), .G_out(pg_cell_80_g_out),
    .P_out(pg_cell_80_p_out));
  pg_cell pg_cell_81 (
    .G(pg_cell_80_g_out), .P(pg_cell_80_p_out), .G_prev(pg_cell_88_g_out), .P_Prev(pg_cell_88_p_out),
    .G_out(pg_cell_81_g_out), .P_out(pg_cell_81_p_out));
  pg_cell pg_cell_82 (
    .G(pg_cell_81_g_out), .P(pg_cell_81_p_out), .G_prev(pg_cell_97_g_out), .P_Prev(pg_cell_97_p_out),
    .G_out(pg_cell_82_g_out), .P_out(pg_cell_82_p_out));
  pg_cell pg_cell_83 (
    .G(pg_cell_82_g_out), .P(pg_cell_82_p_out), .G_prev(pg_cell_108_g_out), .P_Prev(pg_cell_108_p_out),
    .G_out(pg_cell_83_g_out), .P_out(pg_cell_83_p_out));
  koggle_stone_1b bit11 (.A(A[11]), .B(B[11]), .C_in(pg_cell_91_g_out), .g(bit11_g), .p(bit11_p), .sum(SUM11));
  pg_cell pg_cell_84 (
    .G(bit11_g), .P(bit11_p), .G_prev(bit10_g), .P_Prev(bit10_p), .G_out(pg_cell_84_g_out),
    .P_out(pg_cell_84_p_out));
  pg_cell pg_cell_85 (
    .G(pg_cell_84_g_out), .P(pg_cell_84_p_out), .G_prev(pg_cell_92_g_out), .P_Prev(pg_cell_92_p_out),
    .G_out(pg_cell_85_g_out), .P_out(pg_cell_85_p_out));
  pg_cell pg_cell_86 (
    .G(pg_cell_85_g_out), .P(pg_cell_85_p_out), .G_prev(s2_7_g_out), .P_Prev(s2_7_p_out),
    .G_out(pg_cell_86_g_out), .P_out(pg_cell_86_p_out));
  pg_cell pg_cell_87 (
    .G(pg_cell_86_g_out), .P(pg_cell_86_p_out), .G_prev(pg_cell_110_g_out), .P_Prev(pg_cell_110_p_out),
    .G_out(pg_cell_87_g_out), .P_out(pg_cell_87_p_out));
  koggle_stone_1b bit10 (.A(A[10]), .B(B[10]), .C_in(pg_cell_95_g_out), .g(bit10_g), .p(bit10_p), .sum(SUM10));
  pg_cell pg_cell_88 (
    .G(bit10_g), .P(bit10_p), .G_prev(bit9_g), .P_Prev(bit9_p), .G_out(pg_cell_88_g_out),
    .P_out(pg_cell_88_p_out));
  pg_cell pg_cell_89 (
    .G(pg_cell_88_g_out), .P(pg_cell_88_p_out), .G_prev(pg_cell_96_g_out), .P_Prev(pg_cell_96_p_out),
    .G_out(pg_cell_89_g_out), .P_out(pg_cell_89_p_out));
  pg_cell pg_cell_90 (
    .G(pg_cell_89_g_out), .P(pg_cell_89_p_out), .G_prev(pg_cell_101_g_out), .P_Prev(pg_cell_101_p_out),
    .G_out(pg_cell_90_g_out), .P_out(pg_cell_90_p_out));
  pg_cell pg_cell_91 (
    .G(pg_cell_90_g_out), .P(pg_cell_90_p_out), .G_prev(pg_cell_112_g_out), .P_Prev(pg_cell_112_p_out),
    .G_out(pg_cell_91_g_out), .P_out(pg_cell_91_p_out));
  koggle_stone_1b bit9 (.A(A[9]), .B(B[9]), .C_in(pg_cell_99_g_out), .g(bit9_g), .p(bit9_p), .sum(SUM9));
  pg_cell pg_cell_92 (
    .G(bit9_g), .P(bit9_p), .G_prev(bit8_g), .P_Prev(bit8_p), .G_out(pg_cell_92_g_out),
    .P_out(pg_cell_92_p_out));
  pg_cell pg_cell_93 (
    .G(pg_cell_92_g_out), .P(pg_cell_92_p_out), .G_prev(s1_7_g_out), .P_Prev(s1_7_p_out),
    .G_out(pg_cell_93_g_out), .P_out(pg_cell_93_p_out));
  pg_cell pg_cell_94 (
    .G(pg_cell_93_g_out), .P(pg_cell_93_p_out), .G_prev(pg_cell_104_g_out), .P_Prev(pg_cell_104_p_out),
    .G_out(pg_cell_94_g_out), .P_out(pg_cell_94_p_out));
  pg_cell pg_cell_95 (
    .G(pg_cell_94_g_out), .P(pg_cell_94_p_out), .G_prev(pg_cell_113_g_out), .P_Prev(pg_cell_113_p_out),
    .G_out(pg_cell_95_g_out), .P_out(pg_cell_95_p_out));
  koggle_stone_1b bit8 (.A(A[8]), .B(B[8]), .C_in(s3_7_g_out), .g(bit8_g), .p(bit8_p), .sum(SUM8));
  pg_cell pg_cell_96 (
    .G(bit8_g), .P(bit8_p), .G_prev(bit7_g), .P_Prev(bit7_p), .G_out(pg_cell_96_g_out),
    .P_out(pg_cell_96_p_out));
  pg_cell pg_cell_97 (
    .G(pg_cell_96_g_out), .P(pg_cell_96_p_out), .G_prev(pg_cell_100_g_out), .P_Prev(pg_cell_100_p_out),
    .G_out(pg_cell_97_g_out), .P_out(pg_cell_97_p_out));
  pg_cell pg_cell_98 (
    .G(pg_cell_97_g_out), .P(pg_cell_97_p_out), .G_prev(pg_cell_107_g_out), .P_Prev(pg_cell_107_p_out),
    .G_out(pg_cell_98_g_out), .P_out(pg_cell_98_p_out));
  pg_cell pg_cell_99 (
    .G(pg_cell_98_g_out), .P(pg_cell_98_p_out), .G_prev(pg_cell_114_g_out), .P_Prev(pg_cell_114_p_out),
    .G_out(pg_cell_99_g_out), .P_out(pg_cell_99_p_out));
  koggle_stone_1b bit7 (.A(A[7]), .B(B[7]), .C_in(pg_cell_102_g_out), .g(bit7_g), .p(bit7_p), .sum(SUM7));
  pg_cell s1_7 (
    .G(bit7_g), .P(bit7_p), .G_prev(koggle_stone_1b_1_g), .P_Prev(koggle_stone_1b_1_p), .G_out(s1_7_g_out),
    .P_out(s1_7_p_out));
  pg_cell s2_7 (
    .G(s1_7_g_out), .P(s1_7_p_out), .G_prev(pg_cell_103_g_out), .P_Prev(pg_cell_103_p_out),
    .G_out(s2_7_g_out), .P_out(s2_7_p_out));
  pg_cell s3_7 (
    .G(s2_7_g_out), .P(s2_7_p_out), .G_prev(pg_cell_110_g_out), .P_Prev(pg_cell_110_p_out),
    .G_out(s3_7_g_out), .P_out(s3_7_p_out));
  koggle_stone_1b koggle_stone_1b_1 (
    .A(A[6]), .B(B[6]), .C_in(pg_cell_105_g_out), .g(koggle_stone_1b_1_g), .p(koggle_stone_1b_1_p), .sum(SUM6));
  pg_cell pg_cell_100 (
    .G(koggle_stone_1b_1_g), .P(koggle_stone_1b_1_p), .G_prev(koggle_stone_1b_2_g),
    .P_Prev(koggle_stone_1b_2_p), .G_out(pg_cell_100_g_out), .P_out(pg_cell_100_p_out));
  pg_cell pg_cell_101 (
    .G(pg_cell_100_g_out), .P(pg_cell_100_p_out), .G_prev(pg_cell_106_g_out), .P_Prev(pg_cell_106_p_out),
    .G_out(pg_cell_101_g_out), .P_out(pg_cell_101_p_out));
  pg_cell pg_cell_102 (
    .G(pg_cell_101_g_out), .P(pg_cell_101_p_out), .G_prev(pg_cell_112_g_out), .P_Prev(pg_cell_112_p_out),
    .G_out(pg_cell_102_g_out), .P_out(pg_cell_102_p_out));
  koggle_stone_1b koggle_stone_1b_2 (
    .A(A[5]), .B(B[5]), .C_in(pg_cell_108_g_out), .g(koggle_stone_1b_2_g), .p(koggle_stone_1b_2_p), .sum(SUM5));
  pg_cell pg_cell_103 (
    .G(koggle_stone_1b_2_g), .P(koggle_stone_1b_2_p), .G_prev(koggle_stone_1b_3_g),
    .P_Prev(koggle_stone_1b_3_p), .G_out(pg_cell_103_g_out), .P_out(pg_cell_103_p_out));
  pg_cell pg_cell_104 (
    .G(pg_cell_103_g_out), .P(pg_cell_103_p_out), .G_prev(pg_cell_109_g_out), .P_Prev(pg_cell_109_p_out),
    .G_out(pg_cell_104_g_out), .P_out(pg_cell_104_p_out));
  pg_cell pg_cell_105 (
    .G(pg_cell_104_g_out), .P(pg_cell_104_p_out), .G_prev(pg_cell_113_g_out), .P_Prev(pg_cell_113_p_out),
    .G_out(pg_cell_105_g_out), .P_out(pg_cell_105_p_out));
  koggle_stone_1b koggle_stone_1b_3 (
    .A(A[4]), .B(B[4]), .C_in(pg_cell_110_g_out), .g(koggle_stone_1b_3_g), .p(koggle_stone_1b_3_p), .sum(SUM4));
  pg_cell pg_cell_106 (
    .G(koggle_stone_1b_3_g), .P(koggle_stone_1b_3_p), .G_prev(bit3_g), .P_Prev(bit3_p),
    .G_out(pg_cell_106_g_out), .P_out(pg_cell_106_p_out));
  pg_cell pg_cell_107 (
    .G(pg_cell_106_g_out), .P(pg_cell_106_p_out), .G_prev(pg_cell_111_g_out), .P_Prev(pg_cell_111_p_out),
    .G_out(pg_cell_107_g_out), .P_out(pg_cell_107_p_out));
  pg_cell pg_cell_108 (
    .G(pg_cell_107_g_out), .P(pg_cell_107_p_out), .G_prev(pg_cell_114_g_out), .P_Prev(pg_cell_114_p_out),
    .G_out(pg_cell_108_g_out), .P_out(pg_cell_108_p_out));
  koggle_stone_1b bit3 (.A(A[3]), .B(B[3]), .C_in(pg_cell_112_g_out), .g(bit3_g), .p(bit3_p), .sum(SUM3));
  pg_cell pg_cell_109 (
    .G(bit3_g), .P(bit3_p), .G_prev(koggle_stone_1b_4_g), .P_Prev(koggle_stone_1b_4_p),
    .G_out(pg_cell_109_g_out), .P_out(pg_cell_109_p_out));
  pg_cell pg_cell_110 (
    .G(pg_cell_109_g_out), .P(pg_cell_109_p_out), .G_prev(pg_cell_113_g_out), .P_Prev(pg_cell_113_p_out),
    .G_out(pg_cell_110_g_out), .P_out(pg_cell_110_p_out));
  koggle_stone_1b koggle_stone_1b_4 (
    .A(A[2]), .B(B[2]), .C_in(pg_cell_113_g_out), .g(koggle_stone_1b_4_g), .p(koggle_stone_1b_4_p), .sum(SUM2));
  pg_cell pg_cell_111 (
    .G(koggle_stone_1b_4_g), .P(koggle_stone_1b_4_p), .G_prev(koggle_stone_1b_5_g),
    .P_Prev(koggle_stone_1b_5_p), .G_out(pg_cell_111_g_out), .P_out(pg_cell_111_p_out));
  pg_cell pg_cell_112 (
    .G(pg_cell_111_g_out), .P(pg_cell_111_p_out), .G_prev(pg_cell_114_g_out), .P_Prev(pg_cell_114_p_out),
    .G_out(pg_cell_112_g_out), .P_out(pg_cell_112_p_out));
  koggle_stone_1b koggle_stone_1b_5 (
    .A(A[1]), .B(B[1]), .C_in(pg_cell_114_g_out), .g(koggle_stone_1b_5_g), .p(koggle_stone_1b_5_p), .sum(sum1));
  pg_cell pg_cell_113 (
    .G(koggle_stone_1b_5_g), .P(koggle_stone_1b_5_p), .G_prev(pg_cell_114_g_out), .P_Prev(pg_cell_114_p_out),
    .G_out(pg_cell_113_g_out), .P_out(pg_cell_113_p_out));
  koggle_stone_1b koggle_stone_1b_6 (
    .A(A[0]), .B(B[0]), .C_in(Cin), .g(koggle_stone_1b_6_g), .p(koggle_stone_1b_6_p), .sum(sum0));
  pg_cell pg_cell_114 (
    .G(koggle_stone_1b_6_g), .P(koggle_stone_1b_6_p), .G_prev(Cin), .P_Prev(1'b0), .G_out(pg_cell_114_g_out),
    .P_out(pg_cell_114_p_out));
endmodule

module ks_32_sub (
  input  [31:0] in_1,
  input  [31:0] in_2,
  input  SUB,
  output [31:0] out_4,
  output out_5
);

  wire [31:0] bit_extender_1_out, xor_1_out;

  assign bit_extender_1_out = {{31{SUB}}, SUB};  // Bit_Extender bit_extender_1
  // Probe on xor_1_out
  assign xor_1_out = in_2 ^ bit_extender_1_out;  // XOR_Gate xor_1, 32 bits wide
  ks_32b ks_32b_1 (
    .A(in_1), .B(xor_1_out), .Cin(SUB), .SUM31(out_4[31]), .SUM30(out_4[30]), .SUM29(out_4[29]),
    .SUM28(out_4[28]), .SUM27(out_4[27]), .SUM26(out_4[26]), .SUM25(out_4[25]), .SUM24(out_4[24]),
    .SUM23(out_4[23]), .SUM22(out_4[22]), .SUM21(out_4[21]), .SUM20(out_4[20]), .SUM19(out_4[19]),
    .SUM18(out_4[18]), .SUM17(out_4[17]), .SUM16(out_4[16]), .SUM15(out_4[15]), .SUM14(out_4[14]),
    .SUM13(out_4[13]), .SUM12(out_4[12]), .SUM11(out_4[11]), .SUM10(out_4[10]), .SUM9(out_4[9]),
    .SUM8(out_4[8]), .SUM7(out_4[7]), .SUM6(out_4[6]), .SUM5(out_4[5]), .SUM4(out_4[4]), .SUM3(out_4[3]),
    .SUM2(out_4[2]), .sum1(out_4[1]), .sum0(out_4[0]), .Cout(out_5));
endmodule
